// Logisim project ALU.circ as structural Verilog: 1 circuit, main circuit ALU
module ALU (
  input  [31:0] Operand1__rs1,
  input  [31:0] Operand2__rs2,
  input  [3:0] ALUOp,
  input  SignedCmp,
  input  Clock,
  output [31:0] Resultado,
  output Zero,
  output LessThanZero,
  output GreaterThanZero
);

  wire comparator_1_lt, comparator_2_lt, comparator_3_eq, comparator_3_gt, comparator_3_lt, comparator_4_eq,
       comparator_4_gt, comparator_4_lt;
  wire [31:0] adder_1_out, adder_2_out, and_1_out, bit_extender_1_out, bit_extender_2_out, divider_1_out,
       multiplier_1_out, nand_1_out, nor_1_out, not_1_out, or_1_out, shifter_1_out, shifter_2_out,
       shifter_3_out, subtractor_1_out, subtractor_2_out, xor_1_out;

  Subtractor #(.width(32)) subtractor_1 (.a({32{1'b1}}), .b(Operand2__rs2), .out(subtractor_1_out));  // open: bin, bout
  Adder #(.width(32)) adder_1 (.a(Operand1__rs1), .b(Operand2__rs2), .out(adder_1_out));  // open: cin, cout
  Subtractor #(.width(32)) subtractor_2 (
    .a(Operand1__rs1), .b(Operand2__rs2), .out(subtractor_2_out));  // open: bin, bout
  Multiplier #(.width(32)) multiplier_1 (
    .a(Operand1__rs1), .b(Operand2__rs2), .out(multiplier_1_out));  // open: cin, cout
  Divider #(.width(32)) divider_1 (.a(Operand1__rs1), .b(Operand2__rs2), .out(divider_1_out));  // open: upper, rem
  assign and_1_out = Operand1__rs1 & Operand2__rs2;  // AND_Gate and_1, 32 bits wide
  assign nand_1_out = ~(Operand1__rs1 & Operand2__rs2);  // NAND_Gate nand_1, 32 bits wide
  assign nor_1_out = ~(Operand1__rs1 | Operand2__rs2);  // NOR_Gate nor_1, 32 bits wide
  assign not_1_out = ~Operand1__rs1;  // NOT_Gate not_1, 32 bits wide
  assign or_1_out = Operand1__rs1 | Operand2__rs2;  // OR_Gate or_1, 32 bits wide
  assign xor_1_out = Operand1__rs1 ^ Operand2__rs2;  // XOR_Gate xor_1, 32 bits wide
  Shifter #(.width(32)) shifter_1 (.in(Operand1__rs1), .\dist (Operand2__rs2[4:0]), .out(shifter_1_out));
  Shifter #(.width(32), .shift("lr")) shifter_2 (.in(Operand1__rs1), .\dist (Operand2__rs2[4:0]), .out(shifter_2_out));
  Shifter #(.width(32), .shift("ar")) shifter_3 (.in(Operand1__rs1), .\dist (Operand2__rs2[4:0]), .out(shifter_3_out));
  Comparator #(.width(32)) comparator_1 (.a(Operand1__rs1), .b(Operand2__rs2), .lt(comparator_1_lt));  // open: gt, eq
  Comparator #(.width(32), .mode("unsigned")) comparator_2 (
    .a(Operand1__rs1), .b(Operand2__rs2), .lt(comparator_2_lt));  // open: gt, eq
  Adder #(.width(32)) adder_2 (.a(32'h1), .b(subtractor_1_out), .out(adder_2_out));  // open: cin, cout
  assign bit_extender_1_out = {{31{1'b0}}, comparator_1_lt};  // Bit_Extender bit_extender_1
  assign bit_extender_2_out = {{31{1'b0}}, comparator_2_lt};  // Bit_Extender bit_extender_2
  Multiplexer #(.select(4), .width(32), .enable("false")) multiplexer_1 (
    .in0(adder_1_out), .in1(subtractor_2_out), .in2(multiplier_1_out), .in3(divider_1_out), .in4(and_1_out),
    .in5(nand_1_out), .in6(nor_1_out), .in7(not_1_out), .in8(or_1_out), .in9(xor_1_out),
    .in10(shifter_1_out), .in11(shifter_2_out), .in12(shifter_3_out), .in13(bit_extender_1_out),
    .in14(bit_extender_2_out), .in15(adder_2_out), .out(Resultado), .sel(ALUOp));
  Comparator #(.width(32)) comparator_3 (
    .a(Resultado), .b({32{1'b0}}), .gt(comparator_3_gt), .eq(comparator_3_eq), .lt(comparator_3_lt));
  Comparator #(.width(32)) comparator_4 (
    .a(Resultado), .b({32{1'b0}}), .gt(comparator_4_gt), .eq(comparator_4_eq), .lt(comparator_4_lt));
  Multiplexer #(.enable("false")) multiplexer_2 (
    .in0(comparator_3_gt), .in1(comparator_4_gt), .out(GreaterThanZero), .sel(SignedCmp));
  Multiplexer #(.enable("false")) multiplexer_3 (
    .in0(comparator_3_eq), .in1(comparator_4_eq), .out(Zero), .sel(SignedCmp));
  Multiplexer #(.enable("false")) multiplexer_4 (
    .in0(comparator_3_lt), .in1(comparator_4_lt), .out(LessThanZero), .sel(SignedCmp));

  // Other names for the same wires on the sheet: Opeand1[31:0] = Operand1__rs1; Opeand2[31:0] = Operand2__rs2

  // Notes on the sheet:
  //   Datapath
  //   Control
  //   rs1
  //   rs2
  //   Entradas
  //   NEG
  //   Datapath
  //   Salidas
  //   ADD
  //   SUB
  //   MUL
  //   DIV
  //   AND
  //   NAND
  //   NOR
  //   NOT
  //   OR
  //   XOR
  //   SLL
  //   SRL
  //   SRA
  //   SLT
  //   SLTU
endmodule
