// Logisim project ControlUnit_ParteB.circ as structural Verilog: 1 circuit, main circuit ControlUnit
module ControlUnit (
  input  [31:0] instr,
  input  Clock,
  output MemToReg,
  output RegWrite,
  output MemRead,
  output MemWrite,
  output [1:0] Load_Store_type,
  output [1:0] BranchCode,
  output PCSrc,
  output [3:0] ALUOp,
  output [1:0] ALUSrc,
  output BranchOrJump,
  output SignedOp
);

  wire and_8_out, and_9_out, and_10_out, and_11_out, and_12_out, and_13_out, and_14_out, and_15_out,
       and_16_out, and_17_out, and_18_out, and_19_out, and_20_out, and_21_out, and_22_out, and_23_out,
       and_24_out, and_25_out, and_26_out, and_27_out, and_28_out, and_29_out, and_30_out, and_31_out,
       and_32_out, and_33_out, and_34_out, and_35_out, and_36_out, BGE_out, BLT_out, BNE_out,
       comparator_1_eq, comparator_2_eq, comparator_3_eq, demultiplexer_1_out1, demultiplexer_1_out2,
       demultiplexer_1_out3, not_1_out, not_2_out, not_3_out, not_4_out, or_1_out, or_2_out, or_3_out,
       or_4_out, or_10_out, or_13_out, Type_I, Type_R;
  wire [1:0] Type;
  wire [3:0] bit_extender_1_out, bit_extender_2_out, transistor_3_out, transistor_4_out;

  and and_1 (Type_R, instr[0], instr[1], ~instr[2], ~instr[3], instr[4], instr[5], ~instr[6]);  // AND_Gate
  and and_2 (Type_I, instr[0], instr[1], ~instr[2], ~instr[3], instr[4], ~instr[5], ~instr[6]);  // AND_Gate
  and and_3 (MemRead, instr[0], instr[1], ~instr[2], ~instr[3], ~instr[4], ~instr[5], ~instr[6]);  // AND_Gate
  and and_4 (ALUSrc[1], instr[0], instr[1], ~instr[2], ~instr[3], ~instr[4], instr[5], ~instr[6]);  // AND_Gate
  and and_5 (SignedOp, instr[0], instr[1], ~instr[2], ~instr[3], ~instr[4], instr[5], instr[6]);  // AND_Gate
  and and_6 (BranchOrJump, instr[0], instr[1], instr[2], instr[3], ~instr[4], instr[5], instr[6]);  // AND_Gate
  or or_1 (or_1_out, Type_I, MemRead, ALUSrc[1]);
  or or_2 (or_2_out, SignedOp, BranchOrJump);
  or or_3 (or_3_out, Type_R, Type_I, MemRead);
  or or_4 (or_4_out, SignedOp, BranchOrJump);
  and BNE (BNE_out, instr[12], ~instr[13], ~instr[14]);  // AND_Gate
  and BGE (BGE_out, instr[12], ~instr[13], instr[14]);  // AND_Gate
  and BLT (BLT_out, ~instr[12], ~instr[13], instr[14]);  // AND_Gate
  or or_5 (ALUSrc[0], Type_I, MemRead);
  or or_6 (MemToReg, MemRead, ALUSrc[1]);
  and and_7 (RegWrite, or_3_out, ~or_4_out);  // AND_Gate
  or or_7 (BranchCode[0], BNE_out, BGE_out);
  or or_8 (BranchCode[1], BGE_out, BLT_out);
  or or_9 (PCSrc, SignedOp, BranchOrJump);
  or or_10 (or_10_out, MemRead, ALUSrc[1]);
  Multiplexer #(.width(2), .enable("false")) multiplexer_1 (
    .in0(2'b00), .in1(instr[13:12]), .out(Load_Store_type), .sel(or_10_out));
  or or_11 (Type[0], Type_R, or_2_out);
  or or_12 (Type[1], or_1_out, or_2_out);
  Demultiplexer #(.select(2), .enable("false")) demultiplexer_1 (
    .out1(demultiplexer_1_out1), .out2(demultiplexer_1_out2), .out3(demultiplexer_1_out3), .in(1'b1),
    .sel(Type));  // open: out0
  Comparator #(.width(7), .mode("unsigned")) comparator_1 (
    .a(instr[6:0]), .b(7'b0100011), .eq(comparator_1_eq));  // open: gt, lt
  Comparator #(.width(7), .mode("unsigned")) comparator_2 (
    .a(instr[6:0]), .b(7'b0000011), .eq(comparator_2_eq));  // open: gt, lt
  Comparator #(.width(7), .mode("unsigned")) comparator_3 (
    .a(instr[6:0]), .b(7'b1101111), .eq(comparator_3_eq));  // open: gt, lt
  or or_13 (or_13_out, comparator_1_eq, comparator_2_eq);
  and and_8 (and_8_out, ~instr[25], ~instr[26], ~instr[27], ~instr[28], ~instr[29], ~instr[30], ~instr[31]);  // AND_Gate
  and and_9 (and_9_out, ~instr[12], ~instr[13], ~instr[14]);  // AND_Gate
  and and_10 (and_10_out, instr[12], instr[13], instr[14]);
  and and_11 (and_11_out, ~instr[12], instr[13], instr[14]);  // AND_Gate
  and and_12 (and_12_out, ~instr[12], ~instr[13], instr[14]);  // AND_Gate
  and and_13 (and_13_out, instr[12], ~instr[13], ~instr[14]);  // AND_Gate
  and and_14 (and_14_out, instr[12], ~instr[13], instr[14]);  // AND_Gate
  and and_15 (and_15_out, ~instr[12], instr[13], ~instr[14]);  // AND_Gate
  and and_16 (and_16_out, instr[12], instr[13], ~instr[14]);  // AND_Gate
  and and_17 (and_17_out, ~instr[25], ~instr[26], ~instr[27], ~instr[28], ~instr[29], instr[30], ~instr[31]);  // AND_Gate
  and and_18 (and_18_out, ~instr[12], ~instr[13], ~instr[14]);  // AND_Gate
  and and_19 (and_19_out, instr[12], ~instr[13], instr[14]);  // AND_Gate
  and and_20 (and_20_out, instr[25], ~instr[26], ~instr[27], ~instr[28], ~instr[29], ~instr[30], ~instr[31]);  // AND_Gate
  and and_21 (and_21_out, ~instr[12], ~instr[13], ~instr[14]);  // AND_Gate
  and and_22 (and_22_out, ~instr[12], ~instr[13], instr[14]);  // AND_Gate
  not not_1 (not_1_out, or_13_out);
  assign bit_extender_1_out = {{3{1'b0}}, not_1_out};  // Bit_Extender bit_extender_1
  not not_2 (not_2_out, or_13_out);
  and and_23 (and_23_out, not_2_out, demultiplexer_1_out2);
  not not_3 (not_3_out, comparator_3_eq);
  assign bit_extender_2_out = {{3{1'b0}}, not_3_out};  // Bit_Extender bit_extender_2
  not not_4 (not_4_out, comparator_3_eq);
  and and_24 (and_24_out, not_4_out, demultiplexer_1_out3);
  and and_25 (and_25_out, and_8_out, and_9_out);
  and and_26 (and_26_out, and_8_out, and_10_out);
  and and_27 (and_27_out, and_8_out, and_11_out);
  and and_28 (and_28_out, and_8_out, and_12_out);
  and and_29 (and_29_out, and_8_out, and_13_out);
  and and_30 (and_30_out, and_8_out, and_14_out);
  and and_31 (and_31_out, and_8_out, and_15_out);
  and and_32 (and_32_out, and_8_out, and_16_out);
  and and_33 (and_33_out, and_17_out, and_18_out);
  and and_34 (and_34_out, and_17_out, and_19_out);
  and and_35 (and_35_out, and_20_out, and_21_out);
  and and_36 (and_36_out, and_20_out, and_22_out);
  Transistor #(.\type ("n"), .gate("br"), .width(4)) transistor_1 (
    .in(bit_extender_1_out), .out(ALUOp), .gate(or_13_out));
  Transistor #(.\type ("n"), .gate("br"), .width(4)) transistor_2 (
    .in(bit_extender_2_out), .out(ALUOp), .gate(comparator_3_eq));
  Transistor #(.\type ("n"), .width(4)) transistor_3 (.in(4'b0000), .out(transistor_3_out), .gate(and_25_out));
  Transistor #(.\type ("n"), .gate("br"), .width(4)) transistor_4 (
    .in(4'b0000), .out(transistor_4_out), .gate(and_9_out));
  Transistor #(.\type ("n"), .width(4)) transistor_5 (.in(4'b0100), .out(transistor_3_out), .gate(and_26_out));
  Transistor #(.\type ("n"), .gate("br"), .width(4)) transistor_6 (
    .in(4'b0100), .out(transistor_4_out), .gate(and_10_out));
  Transistor #(.\type ("n"), .width(4)) transistor_7 (.in(4'b1000), .out(transistor_3_out), .gate(and_27_out));
  Transistor #(.\type ("n"), .gate("br"), .width(4)) transistor_8 (
    .in(4'b1000), .out(transistor_4_out), .gate(and_11_out));
  Transistor #(.\type ("n"), .width(4)) transistor_9 (.in(4'b1001), .out(transistor_3_out), .gate(and_28_out));
  Transistor #(.\type ("n"), .gate("br"), .width(4)) transistor_10 (
    .in(4'b1001), .out(transistor_4_out), .gate(and_12_out));
  Transistor #(.\type ("n"), .width(4)) transistor_11 (.in(4'b1010), .out(transistor_3_out), .gate(and_29_out));
  Transistor #(.\type ("n"), .gate("br"), .width(4)) transistor_12 (
    .in(4'b1010), .out(transistor_4_out), .gate(and_29_out));
  Transistor #(.\type ("n"), .width(4)) transistor_13 (.in(4'b1011), .out(transistor_3_out), .gate(and_30_out));
  Transistor #(.\type ("n"), .gate("br"), .width(4)) transistor_14 (
    .in(4'b1011), .out(transistor_4_out), .gate(and_30_out));
  Transistor #(.\type ("n"), .width(4)) transistor_15 (.in(4'b1101), .out(transistor_3_out), .gate(and_31_out));
  Transistor #(.\type ("n"), .gate("br"), .width(4)) transistor_16 (
    .in(4'b1101), .out(transistor_4_out), .gate(and_15_out));
  Transistor #(.\type ("n"), .width(4)) transistor_17 (.in(4'b1110), .out(transistor_3_out), .gate(and_32_out));
  Transistor #(.\type ("n"), .gate("br"), .width(4)) transistor_18 (
    .in(4'b1110), .out(transistor_4_out), .gate(and_16_out));
  Transistor #(.\type ("n"), .width(4)) transistor_19 (.in(4'b0001), .out(transistor_3_out), .gate(and_33_out));
  Transistor #(.\type ("n"), .width(4)) transistor_20 (.in(4'b1100), .out(transistor_3_out), .gate(and_34_out));
  Transistor #(.\type ("n"), .gate("br"), .width(4)) transistor_21 (
    .in(4'b1100), .out(transistor_4_out), .gate(and_34_out));
  Transistor #(.\type ("n"), .width(4)) transistor_22 (.in(4'b0010), .out(transistor_3_out), .gate(and_35_out));
  Transistor #(.\type ("n"), .width(4)) transistor_23 (.in(4'b0011), .out(transistor_3_out), .gate(and_36_out));
  Transistor #(.\type ("n"), .gate("br"), .width(4)) transistor_24 (
    .in(transistor_3_out), .out(ALUOp), .gate(demultiplexer_1_out1));
  Transistor #(.\type ("n"), .gate("br"), .width(4)) transistor_25 (
    .in(transistor_4_out), .out(ALUOp), .gate(and_23_out));
  Transistor #(.\type ("n"), .gate("br"), .width(4)) transistor_26 (.in(4'b0001), .out(ALUOp), .gate(and_24_out));

  assign MemWrite = ALUSrc[1];

  // Other names for the same wires on the sheet: funct3[2:0] = instr[14:12]; Store = ALUSrc[1]; Branch = SignedOp;
  //   OpCode[6:0] = instr[6:0]; OpCode4[3:0] = instr[3:0]; OpCode3[2:0] = instr[6:4]; funct7[6:0] = instr[31:25];
  //   Jump = BranchOrJump; Load = MemRead

  // Notes on the sheet:
  //   Entradas
  //   Salidas
  //   Type para calcular  ALUOp
  //   Funct7 = 0000000
  //   Funct7 = 0100000
  //   Funct7 = 0000001
  //   STORE
  //   LOAD
  //   JUMP/JAL
  //   ADD
  //   ADDI
  //   AND
  //   ANDI
  //   OR
  //   ORI
  //   XOR
  //   XORI
  //   SLL
  //   SLLI
  //   SRL
  //   SRLI
  //   SLT
  //   SLTI
  //   SLTU
  //   SLTUI
  //   SUB
  //   SRA
  //   SRAI
  //   MUL
  //   DIV
  //   BRANCH
endmodule
