// Logisim project RegisterFile_B94560.circ as structural Verilog: 1 circuit, main circuit RegisterFile
module RegisterFile (
  input  Clock,
  input  RegWrite,
  input  [4:0] rs1,
  input  [4:0] rs2,
  input  [4:0] Write_register,
  input  [31:0] Write_data,
  output [31:0] d1,
  output [31:0] d2
);

  wire demultiplexer_2_out0, demultiplexer_2_out1, demultiplexer_2_out2, demultiplexer_2_out3,
       demultiplexer_2_out4, demultiplexer_2_out5, demultiplexer_2_out6, demultiplexer_2_out7,
       demultiplexer_2_out8, demultiplexer_2_out9, demultiplexer_2_out10, demultiplexer_2_out11,
       demultiplexer_2_out12, demultiplexer_2_out13, demultiplexer_2_out14, demultiplexer_2_out15,
       demultiplexer_2_out16, demultiplexer_2_out17, demultiplexer_2_out18, demultiplexer_2_out19,
       demultiplexer_2_out20, demultiplexer_2_out21, demultiplexer_2_out22, demultiplexer_2_out23,
       demultiplexer_2_out24, demultiplexer_2_out25, demultiplexer_2_out26, demultiplexer_2_out27,
       demultiplexer_2_out28, demultiplexer_2_out29, demultiplexer_2_out30, demultiplexer_2_out31;
  wire [31:0] demultiplexer_1_out1, demultiplexer_1_out2, demultiplexer_1_out3, demultiplexer_1_out4,
       demultiplexer_1_out5, demultiplexer_1_out6, demultiplexer_1_out7, demultiplexer_1_out8,
       demultiplexer_1_out9, demultiplexer_1_out10, demultiplexer_1_out11, demultiplexer_1_out12,
       demultiplexer_1_out13, demultiplexer_1_out14, demultiplexer_1_out15, demultiplexer_1_out16,
       demultiplexer_1_out17, demultiplexer_1_out18, demultiplexer_1_out19, demultiplexer_1_out20,
       demultiplexer_1_out21, demultiplexer_1_out22, demultiplexer_1_out23, demultiplexer_1_out24,
       demultiplexer_1_out25, demultiplexer_1_out26, demultiplexer_1_out27, demultiplexer_1_out28,
       demultiplexer_1_out29, demultiplexer_1_out30, demultiplexer_1_out31, R1_q, R2_q, R3_q, R4_q, R5_q,
       R6_q, R7_q, R8_q, R9_q, R10_q, R11_q, R12_q, R13_q, R14_q, R15_q, R16_q, R17_q, R18_q, R19_q, R20_q,
       R21_q, R22_q, R23_q, R24_q, R25_q, R26_q, R27_q, R28_q, R29_q, R30_q, R31_q;

  Demultiplexer #(.select(5), .width(32), .enable("false")) demultiplexer_1 (
    .out1(demultiplexer_1_out1), .out2(demultiplexer_1_out2), .out3(demultiplexer_1_out3),
    .out4(demultiplexer_1_out4), .out5(demultiplexer_1_out5), .out6(demultiplexer_1_out6),
    .out7(demultiplexer_1_out7), .out8(demultiplexer_1_out8), .out9(demultiplexer_1_out9),
    .out10(demultiplexer_1_out10), .out11(demultiplexer_1_out11), .out12(demultiplexer_1_out12),
    .out13(demultiplexer_1_out13), .out14(demultiplexer_1_out14), .out15(demultiplexer_1_out15),
    .out16(demultiplexer_1_out16), .out17(demultiplexer_1_out17), .out18(demultiplexer_1_out18),
    .out19(demultiplexer_1_out19), .out20(demultiplexer_1_out20), .out21(demultiplexer_1_out21),
    .out22(demultiplexer_1_out22), .out23(demultiplexer_1_out23), .out24(demultiplexer_1_out24),
    .out25(demultiplexer_1_out25), .out26(demultiplexer_1_out26), .out27(demultiplexer_1_out27),
    .out28(demultiplexer_1_out28), .out29(demultiplexer_1_out29), .out30(demultiplexer_1_out30),
    .out31(demultiplexer_1_out31), .in(Write_data), .sel(Write_register));  // open: out0
  Register #(.width(32), .trigger("high"), .Select("low")) R31 (
    .D(demultiplexer_1_out31), .en(demultiplexer_2_out31), .Q(R31_q), .clk(Clock));  // open: clr
  Register #(.width(32), .trigger("high"), .Select("low")) R1 (
    .D(demultiplexer_1_out1), .en(demultiplexer_2_out1), .Q(R1_q), .clk(Clock));  // open: clr
  Register #(.width(32), .trigger("high"), .Select("low")) R30 (
    .D(demultiplexer_1_out30), .en(demultiplexer_2_out30), .Q(R30_q), .clk(Clock));  // open: clr
  Register #(.width(32), .trigger("high"), .Select("low")) R2 (
    .D(demultiplexer_1_out2), .en(demultiplexer_2_out2), .Q(R2_q), .clk(Clock));  // open: clr
  Register #(.width(32), .trigger("high"), .Select("low")) R29 (
    .D(demultiplexer_1_out29), .en(demultiplexer_2_out29), .Q(R29_q), .clk(Clock));  // open: clr
  Register #(.width(32), .trigger("high"), .Select("low")) R3 (
    .D(demultiplexer_1_out3), .en(demultiplexer_2_out3), .Q(R3_q), .clk(Clock));  // open: clr
  Register #(.width(32), .trigger("high"), .Select("low")) R28 (
    .D(demultiplexer_1_out28), .en(demultiplexer_2_out28), .Q(R28_q), .clk(Clock));  // open: clr
  Register #(.width(32), .trigger("high"), .Select("low")) R4 (
    .D(demultiplexer_1_out4), .en(demultiplexer_2_out4), .Q(R4_q), .clk(Clock));  // open: clr
  Register #(.width(32), .trigger("high"), .Select("low")) R27 (
    .D(demultiplexer_1_out27), .en(demultiplexer_2_out27), .Q(R27_q), .clk(Clock));  // open: clr
  Register #(.width(32), .trigger("high"), .Select("low")) R5 (
    .D(demultiplexer_1_out5), .en(demultiplexer_2_out5), .Q(R5_q), .clk(Clock));  // open: clr
  Register #(.width(32), .trigger("high"), .Select("low")) R26 (
    .D(demultiplexer_1_out26), .en(demultiplexer_2_out26), .Q(R26_q), .clk(Clock));  // open: clr
  Register #(.width(32), .trigger("high"), .Select("low")) R6 (
    .D(demultiplexer_1_out6), .en(demultiplexer_2_out6), .Q(R6_q), .clk(Clock));  // open: clr
  Register #(.width(32), .trigger("high"), .Select("low")) R25 (
    .D(demultiplexer_1_out25), .en(demultiplexer_2_out25), .Q(R25_q), .clk(Clock));  // open: clr
  Register #(.width(32), .trigger("high"), .Select("low")) R7 (
    .D(demultiplexer_1_out7), .en(demultiplexer_2_out7), .Q(R7_q), .clk(Clock));  // open: clr
  Register #(.width(32), .trigger("high"), .Select("low")) R8 (
    .D(demultiplexer_1_out8), .en(demultiplexer_2_out8), .Q(R8_q), .clk(Clock));  // open: clr
  Register #(.width(32), .trigger("high"), .Select("low")) R23 (
    .D(demultiplexer_1_out23), .en(demultiplexer_2_out23), .Q(R23_q), .clk(Clock));  // open: clr
  Register #(.width(32), .trigger("high"), .Select("low")) R24 (
    .D(demultiplexer_1_out24), .en(demultiplexer_2_out24), .Q(R24_q), .clk(Clock));  // open: clr
  Register #(.width(32), .trigger("high"), .Select("low")) R9 (
    .D(demultiplexer_1_out9), .en(demultiplexer_2_out9), .Q(R9_q), .clk(Clock));  // open: clr
  Register #(.width(32), .trigger("high"), .Select("low")) R22 (
    .D(demultiplexer_1_out22), .en(demultiplexer_2_out22), .Q(R22_q), .clk(Clock));  // open: clr
  Register #(.width(32), .trigger("high"), .Select("low")) R10 (
    .D(demultiplexer_1_out10), .en(demultiplexer_2_out10), .Q(R10_q), .clk(Clock));  // open: clr
  Register #(.width(32), .trigger("high"), .Select("low")) R21 (
    .D(demultiplexer_1_out21), .en(demultiplexer_2_out21), .Q(R21_q), .clk(Clock));  // open: clr
  Register #(.width(32), .trigger("high"), .Select("low")) R11 (
    .D(demultiplexer_1_out11), .en(demultiplexer_2_out11), .Q(R11_q), .clk(Clock));  // open: clr
  Register #(.width(32), .trigger("high"), .Select("low")) R20 (
    .D(demultiplexer_1_out20), .en(demultiplexer_2_out20), .Q(R20_q), .clk(Clock));  // open: clr
  Register #(.width(32), .trigger("high"), .Select("low")) R12 (
    .D(demultiplexer_1_out12), .en(demultiplexer_2_out12), .Q(R12_q), .clk(Clock));  // open: clr
  Register #(.width(32), .trigger("high"), .Select("low")) R19 (
    .D(demultiplexer_1_out19), .en(demultiplexer_2_out19), .Q(R19_q), .clk(Clock));  // open: clr
  Register #(.width(32), .trigger("high"), .Select("low")) R13 (
    .D(demultiplexer_1_out13), .en(demultiplexer_2_out13), .Q(R13_q), .clk(Clock));  // open: clr
  Register #(.width(32), .trigger("high"), .Select("low")) R18 (
    .D(demultiplexer_1_out18), .en(demultiplexer_2_out18), .Q(R18_q), .clk(Clock));  // open: clr
  Register #(.width(32), .trigger("high"), .Select("low")) R14 (
    .D(demultiplexer_1_out14), .en(demultiplexer_2_out14), .Q(R14_q), .clk(Clock));  // open: clr
  Register #(.width(32), .trigger("high"), .Select("low")) R17 (
    .D(demultiplexer_1_out17), .en(demultiplexer_2_out17), .Q(R17_q), .clk(Clock));  // open: clr
  Register #(.width(32), .trigger("high"), .Select("low")) R15 (
    .D(demultiplexer_1_out15), .en(demultiplexer_2_out15), .Q(R15_q), .clk(Clock));  // open: clr
  Register #(.width(32), .trigger("high"), .Select("low")) R16 (
    .D(demultiplexer_1_out16), .en(demultiplexer_2_out16), .Q(R16_q), .clk(Clock));  // open: clr
  Demultiplexer #(.select(5), .enable("false")) demultiplexer_2 (
    .out0(demultiplexer_2_out0), .out1(demultiplexer_2_out1), .out2(demultiplexer_2_out2),
    .out3(demultiplexer_2_out3), .out4(demultiplexer_2_out4), .out5(demultiplexer_2_out5),
    .out6(demultiplexer_2_out6), .out7(demultiplexer_2_out7), .out8(demultiplexer_2_out8),
    .out9(demultiplexer_2_out9), .out10(demultiplexer_2_out10), .out11(demultiplexer_2_out11),
    .out12(demultiplexer_2_out12), .out13(demultiplexer_2_out13), .out14(demultiplexer_2_out14),
    .out15(demultiplexer_2_out15), .out16(demultiplexer_2_out16), .out17(demultiplexer_2_out17),
    .out18(demultiplexer_2_out18), .out19(demultiplexer_2_out19), .out20(demultiplexer_2_out20),
    .out21(demultiplexer_2_out21), .out22(demultiplexer_2_out22), .out23(demultiplexer_2_out23),
    .out24(demultiplexer_2_out24), .out25(demultiplexer_2_out25), .out26(demultiplexer_2_out26),
    .out27(demultiplexer_2_out27), .out28(demultiplexer_2_out28), .out29(demultiplexer_2_out29),
    .out30(demultiplexer_2_out30), .out31(demultiplexer_2_out31), .in(RegWrite), .sel(Write_register));
  Multiplexer #(.select(5), .enable("false")) multiplexer_1 (
    .in0(demultiplexer_2_out0), .in1(demultiplexer_2_out1), .in2(demultiplexer_2_out2),
    .in3(demultiplexer_2_out3), .in4(demultiplexer_2_out4), .in5(demultiplexer_2_out5),
    .in6(demultiplexer_2_out6), .in7(demultiplexer_2_out7), .in8(demultiplexer_2_out8),
    .in9(demultiplexer_2_out9), .in10(demultiplexer_2_out10), .in11(demultiplexer_2_out11),
    .in12(demultiplexer_2_out12), .in13(demultiplexer_2_out13), .in14(demultiplexer_2_out14),
    .in15(demultiplexer_2_out15), .in16(demultiplexer_2_out16), .in17(demultiplexer_2_out17),
    .in18(demultiplexer_2_out18), .in19(demultiplexer_2_out19), .in20(demultiplexer_2_out20),
    .in21(demultiplexer_2_out21), .in22(demultiplexer_2_out22), .in23(demultiplexer_2_out23),
    .in24(demultiplexer_2_out24), .in25(demultiplexer_2_out25), .in26(demultiplexer_2_out26),
    .in27(demultiplexer_2_out27), .in28(demultiplexer_2_out28), .in29(demultiplexer_2_out29),
    .in30(demultiplexer_2_out30), .in31(demultiplexer_2_out31));  // open: out, sel
  Multiplexer #(.select(5), .width(32), .enable("false")) multiplexer_2 (
    .in0({32{1'b0}}), .in1(R1_q), .in2(R2_q), .in3(R3_q), .in4(R4_q), .in5(R5_q), .in6(R6_q), .in7(R7_q),
    .in8(R8_q), .in9(R9_q), .in10(R10_q), .in11(R11_q), .in12(R12_q), .in13(R13_q), .in14(R14_q),
    .in15(R15_q), .in16(R16_q), .in17(R17_q), .in18(R18_q), .in19(R19_q), .in20(R20_q), .in21(R21_q),
    .in22(R22_q), .in23(R23_q), .in24(R24_q), .in25(R25_q), .in26(R26_q), .in27(R27_q), .in28(R28_q),
    .in29(R29_q), .in30(R30_q), .in31(R31_q), .out(d1), .sel(rs1));
  Multiplexer #(.select(5), .width(32), .enable("false")) multiplexer_3 (
    .in0({32{1'b0}}), .in1(R1_q), .in2(R2_q), .in3(R3_q), .in4(R4_q), .in5(R5_q), .in6(R6_q), .in7(R7_q),
    .in8(R8_q), .in9(R9_q), .in10(R10_q), .in11(R11_q), .in12(R12_q), .in13(R13_q), .in14(R14_q),
    .in15(R15_q), .in16(R16_q), .in17(R17_q), .in18(R18_q), .in19(R19_q), .in20(R20_q), .in21(R21_q),
    .in22(R22_q), .in23(R23_q), .in24(R24_q), .in25(R25_q), .in26(R26_q), .in27(R27_q), .in28(R28_q),
    .in29(R29_q), .in30(R30_q), .in31(R31_q), .out(d2), .sel(rs2));

  // Notes on the sheet:
  //   Entradas
  //   Salidas
endmodule
