// Logisim project ParteB.circ as structural Verilog: 8 circuits, main circuit Pipeline
module Pipeline (
);

  wire ALU_greaterthanzero, ALU_lessthanzero, ALU_zero, and_1_out, Clock, EX_MEM_mem_greater_than,
       EX_MEM_mem_less_than, EX_MEM_mem_memread, EX_MEM_mem_memtoreg, EX_MEM_mem_memwrite,
       EX_MEM_mem_regwrite, EX_MEM_mem_zero, GE_out, Hazard_Detection_Unit_if_id_write,
       Hazard_Detection_Unit_pcwrite, Hazard_Detection_Unit_stall, ID_EX_ex_branchorjump, ID_EX_ex_memread,
       ID_EX_ex_memtoreg, ID_EX_ex_memwrite, ID_EX_ex_pcsrc, ID_EX_ex_regwrite, ID_EX_ex_signedop,
       MEM_WEB_wb_memtoreg, MEM_WEB_wb_regwrite, multiplexer_8_out, NE_out, not_1_out;
  wire [0:0] IF_ID_id_instruction_5;
  wire [1:0] controlunit_1_alusrc, controlunit_1_branchcode, controlunit_1_load_store_type,
       EX_MEM_mem_branchcode, EX_MEM_mem_load_store_type, ForwardingUnit_forwarda, ForwardingUnit_forwardb,
       ID_EX_ex_alusrc, ID_EX_ex_branchcode;
  wire [3:0] controlunit_1_aluop, ID_EX_ex_aluop;
  wire [4:0] EX_MEM_mem_write_register, ID_EX_ex_write_register, ID_EX_forwarding_rs1, ID_EX_forwarding_rs2,
       IF_ID_id_instruction_2, IF_ID_id_instruction_3, IF_ID_id_instruction_4, MEM_WEB_wb_write_register;
  wire [6:0] IF_ID_id_instruction;
  wire [11:11] IF_ID_id_instruction_7;
  wire [16:0] controlunit_1_memtoreg, multiplexer_3_out;
  wire [19:12] IF_ID_id_instruction_6;
  wire [31:0] adder_1_out, adder_2_out, ALU_resultado, bit_extender_1_out, bit_extender_2_out,
       bit_extender_3_out, bit_extender_4_out, DataMemory_readdata, EX_MEM_mem_address, EX_MEM_mem_pc___4,
       EX_MEM_mem_write_data, ID_EX_ex_imm_branch, ID_EX_ex_imm_jump, ID_EX_ex_imm_lw_xl, ID_EX_ex_imm_sw,
       ID_EX_ex_pc___4, ID_EX_ex_rs1, ID_EX_ex_rs2, IF_ID_id_pc___4, Instruction_Memory_data,
       MEM_WEB_wb_address, MEM_WEB_wb_read_data, multiplexer_1_out, multiplexer_2_out, multiplexer_4_out,
       multiplexer_5_out, multiplexer_6_out, multiplexer_7_out, multiplexer_9_out, PC_q, registerfile_1_d1,
       registerfile_1_d2;

  Clock clock_1 (.out(Clock));
  Multiplexer #(.width(32), .enable("false")) multiplexer_1 (
    .in0(adder_1_out), .in1(multiplexer_2_out), .out(multiplexer_1_out), .sel(ID_EX_ex_pcsrc));
  Register #(.width(32), .Select("low")) PC (
    .D(multiplexer_1_out), .en(Hazard_Detection_Unit_pcwrite), .Q(PC_q), .clk(Clock));  // open: clr
  Adder #(.width(32)) adder_1 (.a(32'h4), .b(PC_q), .out(adder_1_out));  // open: cin, cout
  ROM #(.dataWidth(32), .Select("low")) Instruction_Memory (.addr(PC_q[9:2]), .data(Instruction_Memory_data));
  IF_ID IF_ID (
    .IF_PC___4(adder_1_out), .IF_Instruction(Instruction_Memory_data), .Clock(Clock),
    .ID_PC___4(IF_ID_id_pc___4),
    .ID_Instruction({IF_ID_id_instruction_7[11], IF_ID_id_instruction_4, IF_ID_id_instruction_3, IF_ID_id_instruction_5[0], IF_ID_id_instruction_6, IF_ID_id_instruction_2, IF_ID_id_instruction}),
    .IF_ID_Write(Hazard_Detection_Unit_if_id_write));
  HazardDetectionUnit Hazard_Detection_Unit (
    .ID_EX_rs2(ID_EX_ex_write_register), .IF_ID_rs1(IF_ID_id_instruction_6[19:15]),
    .IF_ID_rs2({IF_ID_id_instruction_3[3:0], IF_ID_id_instruction_5[0]}), .ID_EX_MemRead(ID_EX_ex_memread),
    .IF_ID_Write(Hazard_Detection_Unit_if_id_write), .PCWrite(Hazard_Detection_Unit_pcwrite),
    .Stall(Hazard_Detection_Unit_stall));
  ControlUnit controlunit_1 (
    .instr({IF_ID_id_instruction_7[11], IF_ID_id_instruction_4, IF_ID_id_instruction_3, IF_ID_id_instruction_5[0], IF_ID_id_instruction_6, IF_ID_id_instruction_2, IF_ID_id_instruction}),
    .Clock(Clock), .MemToReg(controlunit_1_memtoreg[0]), .RegWrite(controlunit_1_memtoreg[1]),
    .MemRead(controlunit_1_memtoreg[2]), .MemWrite(controlunit_1_memtoreg[3]),
    .BranchCode(controlunit_1_branchcode), .PCSrc(controlunit_1_memtoreg[8]), .ALUOp(controlunit_1_aluop),
    .ALUSrc(controlunit_1_alusrc), .BranchOrJump(controlunit_1_memtoreg[15]),
    .SignedOp(controlunit_1_memtoreg[16]), .Load_Store_type(controlunit_1_load_store_type));
  and and_1 (and_1_out, multiplexer_8_out, not_1_out);
  Multiplexer #(.width(32), .enable("false")) multiplexer_2 (
    .in0(EX_MEM_mem_pc___4), .in1(adder_2_out), .out(multiplexer_2_out), .sel(and_1_out));
  Multiplexer #(.width(17), .enable("false")) multiplexer_3 (
    .in0({controlunit_1_memtoreg[16:15], controlunit_1_alusrc, controlunit_1_aluop, controlunit_1_memtoreg[8], controlunit_1_branchcode, controlunit_1_load_store_type, controlunit_1_memtoreg[3:0]}),
    .in1({17{1'b0}}), .out(multiplexer_3_out), .sel(Hazard_Detection_Unit_stall));
  not not_1 (not_1_out, ID_EX_ex_branchorjump);
  RegisterFile registerfile_1 (
    .Clock(Clock), .RegWrite(MEM_WEB_wb_regwrite), .rs1(IF_ID_id_instruction_6[19:15]),
    .rs2({IF_ID_id_instruction_3[3:0], IF_ID_id_instruction_5[0]}),
    .Write_register(MEM_WEB_wb_write_register), .Write_data(multiplexer_9_out), .d1(registerfile_1_d1),
    .d2(registerfile_1_d2));
  assign bit_extender_1_out = {{20{1'b0}}, {IF_ID_id_instruction_7[11], IF_ID_id_instruction_4, IF_ID_id_instruction_3, IF_ID_id_instruction_5[0]}};  // Bit_Extender bit_extender_1
  assign bit_extender_2_out = {{20{1'b0}}, {IF_ID_id_instruction_7[11], IF_ID_id_instruction_4, IF_ID_id_instruction_3[4], IF_ID_id_instruction_2}};  // Bit_Extender bit_extender_2
  assign bit_extender_3_out = {{20{1'b0}}, {IF_ID_id_instruction_7[11], IF_ID_id_instruction_2[0], IF_ID_id_instruction_4, IF_ID_id_instruction_2[4:1], 1'b0}};  // Bit_Extender bit_extender_3
  assign bit_extender_4_out = {{11{1'b0}}, {IF_ID_id_instruction_7[11], IF_ID_id_instruction_6, IF_ID_id_instruction_5[0], IF_ID_id_instruction_4, IF_ID_id_instruction_3, 1'b0}};  // Bit_Extender bit_extender_4
  ID_EX ID_EX (
    .ID_PC___4(IF_ID_id_pc___4), .ID_rs1(registerfile_1_d1), .ID_rs2(registerfile_1_d2),
    .ID_Imm_LW_xl(bit_extender_1_out), .ID_Imm_SW(bit_extender_2_out), .ID_Imm_Branch(bit_extender_3_out),
    .ID_Imm_Jump(bit_extender_4_out), .in_22(Clock), .EX_PC___4(ID_EX_ex_pc___4), .EX_rs1(ID_EX_ex_rs1),
    .EX_rs2(ID_EX_ex_rs2), .EX_Imm_LW_xl(ID_EX_ex_imm_lw_xl), .EX_Imm_SW(ID_EX_ex_imm_sw),
    .EX_Imm_Branch(ID_EX_ex_imm_branch), .EX_Imm_Jump(ID_EX_ex_imm_jump),
    .ID_Write_Register(IF_ID_id_instruction_2), .EX_Write_Register(ID_EX_ex_write_register),
    .ID_MemToReg(multiplexer_3_out[0]), .ID_RegWrite(multiplexer_3_out[1]),
    .ID_MemRead(multiplexer_3_out[2]), .ID_MemWrite(multiplexer_3_out[3]),
    .ID_BranchCode(multiplexer_3_out[7:6]), .ID_BranchOrJump(multiplexer_3_out[15]),
    .ID_SignedOp(multiplexer_3_out[16]), .ID_ALUSrc(multiplexer_3_out[14:13]),
    .ID_ALUOp(multiplexer_3_out[12:9]), .ID_PCSrc(multiplexer_3_out[8]), .EX_MemToReg(ID_EX_ex_memtoreg),
    .EX_RegWrite(ID_EX_ex_regwrite), .EX_MemRead(ID_EX_ex_memread), .EX_MemWrite(ID_EX_ex_memwrite),
    .EX_BranchCode(ID_EX_ex_branchcode), .EX_BranchOrJump(ID_EX_ex_branchorjump), .EX_PCSrc(ID_EX_ex_pcsrc),
    .EX_SignedOp(ID_EX_ex_signedop), .EX_ALUSrc(ID_EX_ex_alusrc), .EX_ALUOp(ID_EX_ex_aluop),
    .IF_ID_rs2({IF_ID_id_instruction_3[3:0], IF_ID_id_instruction_5[0]}),
    .IF_ID_rs1(IF_ID_id_instruction_6[19:15]), .Forwarding_rs1(ID_EX_forwarding_rs1),
    .Forwarding_rs2(ID_EX_forwarding_rs2), .ID_Load_Store_type(multiplexer_3_out[5:4]),
    .EX_Load_Store_type(multiplexer_3_out[5:4]));
  Multiplexer #(.width(32), .enable("false")) multiplexer_4 (
    .in0(ID_EX_ex_imm_branch), .in1(ID_EX_ex_imm_jump), .out(multiplexer_4_out), .sel(ID_EX_ex_branchorjump));
  Multiplexer #(.select(2), .width(32), .enable("false")) multiplexer_5 (
    .in0(ID_EX_ex_rs1), .in1(multiplexer_9_out), .in2(EX_MEM_mem_address), .out(multiplexer_5_out),
    .sel(ForwardingUnit_forwarda));  // open: in3
  Multiplexer #(.select(2), .width(32), .enable("false")) multiplexer_6 (
    .in0(ID_EX_ex_rs2), .in1(multiplexer_9_out), .in2(EX_MEM_mem_address), .out(multiplexer_6_out),
    .sel(ForwardingUnit_forwardb));  // open: in3
  ForwardingUnit ForwardingUnit (
    .ID_EX_rs1(ID_EX_forwarding_rs1), .ID_EX_rs2(ID_EX_forwarding_rs2),
    .EX_MEM_WriteRegister(EX_MEM_mem_write_register), .MEM_WB_WriteRegister(MEM_WEB_wb_write_register),
    .EX_MEM_RegWrite(EX_MEM_mem_regwrite), .MEM_WB_RegWrite(MEM_WEB_wb_regwrite),
    .ForwardA(ForwardingUnit_forwarda), .ForwardB(ForwardingUnit_forwardb));
  Adder #(.width(32)) adder_2 (.a(ID_EX_ex_pc___4), .b(multiplexer_4_out), .out(adder_2_out));  // open: cin, cout
  Multiplexer #(.select(2), .width(32), .enable("false")) multiplexer_7 (
    .in0(multiplexer_6_out), .in1(ID_EX_ex_imm_lw_xl), .in2(ID_EX_ex_imm_sw), .out(multiplexer_7_out),
    .sel(ID_EX_ex_alusrc));  // open: in3
  ALU ALU (
    .Operand1__rs1(multiplexer_5_out), .Operand2__rs2(multiplexer_7_out), .ALUOp(ID_EX_ex_aluop),
    .Clock(Clock), .Resultado(ALU_resultado), .Zero(ALU_zero), .LessThanZero(ALU_lessthanzero),
    .GreaterThanZero(ALU_greaterthanzero), .SignedCmp(ID_EX_ex_signedop));
  EX_MEM EX_MEM (
    .EX_PC___4(adder_2_out), .EX_Zero(ALU_zero), .EX_Address(ALU_resultado),
    .EX_Write_Data(multiplexer_6_out), .EX_Write_Register(ID_EX_ex_write_register), .Clock(Clock),
    .MEM_PC___4(EX_MEM_mem_pc___4), .MEM_Zero(EX_MEM_mem_zero), .MEM_Address(EX_MEM_mem_address),
    .MEM_Write_Data(EX_MEM_mem_write_data), .MEM_Write_Register(EX_MEM_mem_write_register),
    .EX_Less_Than(ALU_lessthanzero), .EX_Greater_Than(ALU_greaterthanzero),
    .MEM_Less_Than(EX_MEM_mem_less_than), .MEM_Greater_Than(EX_MEM_mem_greater_than),
    .EX_MemToReg(ID_EX_ex_memtoreg), .MEM_MemToReg(EX_MEM_mem_memtoreg), .EX_RegWrite(ID_EX_ex_regwrite),
    .MEM_RegWrite(EX_MEM_mem_regwrite), .EX_MemRead(ID_EX_ex_memread), .MEM_MemRead(EX_MEM_mem_memread),
    .EX_MemWrite(ID_EX_ex_memwrite), .MEM_MemWrite(EX_MEM_mem_memwrite), .EX_BranchCode(ID_EX_ex_branchcode),
    .MEM_BranchCode(EX_MEM_mem_branchcode), .EX_Load_Store_type(multiplexer_3_out[5:4]),
    .MEM_Load_Store_type(EX_MEM_mem_load_store_type));
  or GE (GE_out, EX_MEM_mem_greater_than, EX_MEM_mem_zero);
  or NE (NE_out, EX_MEM_mem_greater_than, EX_MEM_mem_less_than);
  Multiplexer #(.select(2), .enable("false")) multiplexer_8 (
    .in0(EX_MEM_mem_zero), .in1(NE_out), .in2(EX_MEM_mem_less_than), .in3(GE_out), .out(multiplexer_8_out),
    .sel(EX_MEM_mem_branchcode));
  DataMemory DataMemory (
    .Address(EX_MEM_mem_address), .WriteData(EX_MEM_mem_write_data), .MemRead(EX_MEM_mem_memread),
    .MemWrite(EX_MEM_mem_memwrite), .Clock(Clock), .ReadData(DataMemory_readdata),
    .load_store_type(EX_MEM_mem_load_store_type));
  MEM_WB MEM_WEB (
    .MEM_Read_Data(DataMemory_readdata), .MEM_Address(EX_MEM_mem_address),
    .MEM_Write_Register(EX_MEM_mem_write_register), .Clock(Clock), .WB_Read_Data(MEM_WEB_wb_read_data),
    .WB_Address(MEM_WEB_wb_address), .WB_Write_Register(MEM_WEB_wb_write_register),
    .MEM_MemToReg(EX_MEM_mem_memtoreg), .WB_MemToReg(MEM_WEB_wb_memtoreg),
    .MEM_RegWrite(EX_MEM_mem_regwrite), .WB_RegWrite(MEM_WEB_wb_regwrite));
  Multiplexer #(.width(32), .enable("false")) multiplexer_9 (
    .in0(MEM_WEB_wb_address), .in1(MEM_WEB_wb_read_data), .out(multiplexer_9_out), .sel(MEM_WEB_wb_memtoreg));

  // Notes on the sheet:
  //   contents of Instruction_Memory (hex, n*v repeats v):
  //   110523 218a23 1400183
  //   I-Type/Load
  //   S-Type
  //   Branch
  //   Jump
  //   Write Register
endmodule

module ID_EX (
  input  [31:0] ID_PC___4,
  input  [31:0] ID_rs1,
  input  [31:0] ID_rs2,
  input  [31:0] ID_Imm_LW_xl,
  input  [31:0] ID_Imm_SW,
  input  [31:0] ID_Imm_Branch,
  input  [31:0] ID_Imm_Jump,
  input  [4:0] IF_ID_rs1,
  input  [4:0] IF_ID_rs2,
  input  [4:0] ID_Write_Register,
  input  ID_MemToReg,
  input  ID_RegWrite,
  input  ID_MemRead,
  input  ID_MemWrite,
  input  [1:0] ID_Load_Store_type,
  input  [1:0] ID_BranchCode,
  input  [3:0] ID_ALUOp,
  input  [1:0] ID_ALUSrc,
  input  ID_BranchOrJump,
  input  ID_PCSrc,
  input  ID_SignedOp,
  input  in_22,
  output [31:0] EX_PC___4,
  output [31:0] EX_rs1,
  output [31:0] EX_rs2,
  output [31:0] EX_Imm_LW_xl,
  output [31:0] EX_Imm_SW,
  output [31:0] EX_Imm_Branch,
  output [31:0] EX_Imm_Jump,
  output [4:0] Forwarding_rs1,
  output [4:0] Forwarding_rs2,
  output [4:0] EX_Write_Register,
  output EX_MemToReg,
  output EX_RegWrite,
  output EX_MemRead,
  output EX_MemWrite,
  output [1:0] EX_Load_Store_type,
  output [1:0] EX_BranchCode,
  output [3:0] EX_ALUOp,
  output [1:0] EX_ALUSrc,
  output EX_BranchOrJump,
  output EX_PCSrc,
  output EX_SignedOp
);

  Register #(.width(32), .Select("low")) register_1 (.D(ID_PC___4), .Q(EX_PC___4), .clk(in_22));  // open: en, clr
  Register #(.width(32), .Select("low")) register_2 (.D(ID_rs1), .Q(EX_rs1), .clk(in_22));  // open: en, clr
  Register #(.width(32), .Select("low")) register_3 (.D(ID_rs2), .Q(EX_rs2), .clk(in_22));  // open: en, clr
  Register #(.width(32), .Select("low")) register_4 (.D(ID_Imm_LW_xl), .Q(EX_Imm_LW_xl), .clk(in_22));  // open: en, clr
  Register #(.width(32), .Select("low")) register_5 (.D(ID_Imm_SW), .Q(EX_Imm_SW), .clk(in_22));  // open: en, clr
  Register #(.width(32), .Select("low")) register_6 (
    .D(ID_Imm_Branch), .Q(EX_Imm_Branch), .clk(in_22));  // open: en, clr
  Register #(.width(32), .Select("low")) register_7 (.D(ID_Imm_Jump), .Q(EX_Imm_Jump), .clk(in_22));  // open: en, clr
  Register #(.width(5), .Select("low")) register_8 (.D(IF_ID_rs1), .Q(Forwarding_rs1), .clk(in_22));  // open: en, clr
  Register #(.width(5), .Select("low")) register_9 (.D(IF_ID_rs2), .Q(Forwarding_rs2), .clk(in_22));  // open: en, clr
  Register #(.width(5), .Select("low")) register_10 (
    .D(ID_Write_Register), .Q(EX_Write_Register), .clk(in_22));  // open: en, clr
  Register #(.width(1), .Select("low")) register_11 (.D(ID_MemToReg), .Q(EX_MemToReg), .clk(in_22));  // open: en, clr
  Register #(.width(1), .Select("low")) register_12 (.D(ID_RegWrite), .Q(EX_RegWrite), .clk(in_22));  // open: en, clr
  Register #(.width(1), .Select("low")) register_13 (.D(ID_MemRead), .Q(EX_MemRead), .clk(in_22));  // open: en, clr
  Register #(.width(1), .Select("low")) register_14 (.D(ID_MemWrite), .Q(EX_MemWrite), .clk(in_22));  // open: en, clr
  Register #(.width(2), .Select("low")) register_15 (
    .D(ID_Load_Store_type), .Q(EX_Load_Store_type), .clk(in_22));  // open: en, clr
  Register #(.width(2), .Select("low")) register_16 (
    .D(ID_BranchCode), .Q(EX_BranchCode), .clk(in_22));  // open: en, clr
  Register #(.width(4), .Select("low")) register_17 (.D(ID_ALUOp), .Q(EX_ALUOp), .clk(in_22));  // open: en, clr
  Register #(.width(2), .Select("low")) register_18 (.D(ID_ALUSrc), .Q(EX_ALUSrc), .clk(in_22));  // open: en, clr
  Register #(.width(1), .Select("low")) register_19 (
    .D(ID_BranchOrJump), .Q(EX_BranchOrJump), .clk(in_22));  // open: en, clr
  Register #(.width(1), .Select("low")) register_20 (.D(ID_PCSrc), .Q(EX_PCSrc), .clk(in_22));  // open: en, clr
  Register #(.width(1), .Select("low")) register_21 (.D(ID_SignedOp), .Q(EX_SignedOp), .clk(in_22));  // open: en, clr

  // Other names for the same wires on the sheet: Clock = in_22; SignedOp = ID_SignedOp

  // Notes on the sheet:
  //   Entradas
  //   WB Flags
  //   Mem Flags
  //   EX Flags
  //   Salidas
  //   WB Flags
  //   Mem Flags
  //   EX Flags
endmodule

module IF_ID (
  input  [31:0] IF_PC___4,
  input  [31:0] IF_Instruction,
  input  IF_ID_Write,
  input  Clock,
  output [31:0] ID_PC___4,
  output [31:0] ID_Instruction
);

  Register #(.width(32), .Select("low")) register_1 (
    .D(IF_PC___4), .en(IF_ID_Write), .Q(ID_PC___4), .clk(Clock));  // open: clr
  Register #(.width(32), .Select("low")) register_2 (
    .D(IF_Instruction), .en(IF_ID_Write), .Q(ID_Instruction), .clk(Clock));  // open: clr

  // Other names for the same wires on the sheet: ID_Instr[31:0] = ID_Instruction; ID_PC_4[31:0] = ID_PC___4;
  //   IF_Instr[31:0] = IF_Instruction; IF_PC_4[31:0] = IF_PC___4

  // Notes on the sheet:
  //   Control
endmodule

module EX_MEM (
  input  [31:0] EX_PC___4,
  input  EX_Zero,
  input  EX_Less_Than,
  input  EX_Greater_Than,
  input  [31:0] EX_Address,
  input  [31:0] EX_Write_Data,
  input  [4:0] EX_Write_Register,
  input  EX_MemToReg,
  input  EX_RegWrite,
  input  EX_MemRead,
  input  EX_MemWrite,
  input  [1:0] EX_Load_Store_type,
  input  [1:0] EX_BranchCode,
  input  Clock,
  output [31:0] MEM_PC___4,
  output MEM_Zero,
  output MEM_Less_Than,
  output MEM_Greater_Than,
  output [31:0] MEM_Address,
  output [31:0] MEM_Write_Data,
  output [4:0] MEM_Write_Register,
  output MEM_MemToReg,
  output MEM_RegWrite,
  output MEM_MemRead,
  output MEM_MemWrite,
  output [1:0] MEM_Load_Store_type,
  output [1:0] MEM_BranchCode
);

  Register #(.width(32), .Select("low")) register_1 (.D(EX_PC___4), .Q(MEM_PC___4), .clk(Clock));  // open: en, clr
  Register #(.width(1), .Select("low")) register_2 (.D(EX_Zero), .Q(MEM_Zero), .clk(Clock));  // open: en, clr
  Register #(.width(1), .Select("low")) register_3 (.D(EX_Less_Than), .Q(MEM_Less_Than), .clk(Clock));  // open: en, clr
  Register #(.width(1), .Select("low")) register_4 (
    .D(EX_Greater_Than), .Q(MEM_Greater_Than), .clk(Clock));  // open: en, clr
  Register #(.width(32), .Select("low")) register_5 (.D(EX_Address), .Q(MEM_Address), .clk(Clock));  // open: en, clr
  Register #(.width(32), .Select("low")) register_6 (
    .D(EX_Write_Data), .Q(MEM_Write_Data), .clk(Clock));  // open: en, clr
  Register #(.width(5), .Select("low")) register_7 (
    .D(EX_Write_Register), .Q(MEM_Write_Register), .clk(Clock));  // open: en, clr
  Register #(.width(1), .Select("low")) register_8 (.D(EX_MemToReg), .Q(MEM_MemToReg), .clk(Clock));  // open: en, clr
  Register #(.width(1), .Select("low")) register_9 (.D(EX_RegWrite), .Q(MEM_RegWrite), .clk(Clock));  // open: en, clr
  Register #(.width(1), .Select("low")) register_10 (.D(EX_MemRead), .Q(MEM_MemRead), .clk(Clock));  // open: en, clr
  Register #(.width(1), .Select("low")) register_11 (.D(EX_MemWrite), .Q(MEM_MemWrite), .clk(Clock));  // open: en, clr
  Register #(.width(2), .Select("low")) register_12 (
    .D(EX_Load_Store_type), .Q(MEM_Load_Store_type), .clk(Clock));  // open: en, clr
  Register #(.width(2), .Select("low")) register_13 (
    .D(EX_BranchCode), .Q(MEM_BranchCode), .clk(Clock));  // open: en, clr

  // Notes on the sheet:
  //   WB Flags
  //   Mem Flags
  //   WB Flags
  //   Mem Flags
endmodule

module MEM_WB (
  input  [31:0] MEM_Read_Data,
  input  [31:0] MEM_Address,
  input  [4:0] MEM_Write_Register,
  input  MEM_MemToReg,
  input  MEM_RegWrite,
  input  Clock,
  output [31:0] WB_Read_Data,
  output [31:0] WB_Address,
  output [4:0] WB_Write_Register,
  output WB_MemToReg,
  output WB_RegWrite
);

  Register #(.width(32), .Select("low")) register_1 (
    .D(MEM_Read_Data), .Q(WB_Read_Data), .clk(Clock));  // open: en, clr
  Register #(.width(32), .Select("low")) register_2 (.D(MEM_Address), .Q(WB_Address), .clk(Clock));  // open: en, clr
  Register #(.width(5), .Select("low")) register_3 (
    .D(MEM_Write_Register), .Q(WB_Write_Register), .clk(Clock));  // open: en, clr
  Register #(.width(1), .Select("low")) register_4 (.D(MEM_MemToReg), .Q(WB_MemToReg), .clk(Clock));  // open: en, clr
  Register #(.width(1), .Select("low")) register_5 (.D(MEM_RegWrite), .Q(WB_RegWrite), .clk(Clock));  // open: en, clr

  // Notes on the sheet:
  //   WB Flags
  //   WB Flags
endmodule

module ForwardingUnit (
  input  [4:0] ID_EX_rs1,
  input  [4:0] ID_EX_rs2,
  input  [4:0] EX_MEM_WriteRegister,
  input  [4:0] MEM_WB_WriteRegister,
  input  EX_MEM_RegWrite,
  input  MEM_WB_RegWrite,
  output [1:0] ForwardA,
  output [1:0] ForwardB
);

  wire comparator_1_eq, comparator_2_eq, comparator_3_eq, comparator_4_eq, comparator_5_eq, comparator_6_eq,
       comparator_7_eq, comparator_8_eq;

  Comparator #(.width(5)) comparator_1 (.a(EX_MEM_WriteRegister), .b({5{1'b0}}), .eq(comparator_1_eq));  // open: gt, lt
  Comparator #(.width(5)) comparator_2 (.a(ID_EX_rs1), .b(EX_MEM_WriteRegister), .eq(comparator_2_eq));  // open: gt, lt
  Comparator #(.width(5)) comparator_3 (.a(EX_MEM_WriteRegister), .b({5{1'b0}}), .eq(comparator_3_eq));  // open: gt, lt
  Comparator #(.width(5)) comparator_4 (.a(ID_EX_rs2), .b(EX_MEM_WriteRegister), .eq(comparator_4_eq));  // open: gt, lt
  Comparator #(.width(5)) comparator_5 (.a(MEM_WB_WriteRegister), .b({5{1'b0}}), .eq(comparator_5_eq));  // open: gt, lt
  Comparator #(.width(5)) comparator_6 (.a(ID_EX_rs1), .b(MEM_WB_WriteRegister), .eq(comparator_6_eq));  // open: gt, lt
  Comparator #(.width(5)) comparator_7 (.a(MEM_WB_WriteRegister), .b({5{1'b0}}), .eq(comparator_7_eq));  // open: gt, lt
  Comparator #(.width(5)) comparator_8 (.a(ID_EX_rs2), .b(MEM_WB_WriteRegister), .eq(comparator_8_eq));  // open: gt, lt
  and and_1 (ForwardA[1], EX_MEM_RegWrite, ~comparator_1_eq, comparator_2_eq);  // AND_Gate
  and and_2 (ForwardB[1], EX_MEM_RegWrite, ~comparator_3_eq, comparator_4_eq);  // AND_Gate
  and and_3 (ForwardA[0], MEM_WB_RegWrite, ~comparator_5_eq, comparator_6_eq, ~ForwardA[1]);  // AND_Gate
  and and_4 (ForwardB[0], MEM_WB_RegWrite, ~comparator_7_eq, comparator_8_eq, ~ForwardB[1]);  // AND_Gate

  // Other names for the same wires on the sheet: _2a_Hazard = ForwardA[0]; _1a_Hazard = ForwardA[1];
  //   _2b_Hazard = ForwardB[0]; _1b_Hazard = ForwardB[1]

  // Notes on the sheet:
  //   Entradas
  //   Salidas
endmodule

module HazardDetectionUnit (
  input  [4:0] ID_EX_rs2,
  input  [4:0] IF_ID_rs1,
  input  [4:0] IF_ID_rs2,
  input  ID_EX_MemRead,
  output IF_ID_Write,
  output PCWrite,
  output Stall
);

  wire comparator_1_eq, comparator_2_eq, or_1_out;

  Comparator #(.width(5)) comparator_1 (.a(ID_EX_rs2), .b(IF_ID_rs1), .eq(comparator_1_eq));  // open: gt, lt
  Comparator #(.width(5)) comparator_2 (.a(ID_EX_rs2), .b(IF_ID_rs2), .eq(comparator_2_eq));  // open: gt, lt
  not not_1 (IF_ID_Write, Stall);
  or or_1 (or_1_out, comparator_1_eq, comparator_2_eq);
  and and_1 (Stall, ID_EX_MemRead, or_1_out);

  assign PCWrite = IF_ID_Write;

  // Notes on the sheet:
  //   Entradas
  //   Salidas
endmodule

module DataMemory (
  input  [31:0] Address,
  input  [31:0] WriteData,
  input  MemRead,
  input  MemWrite,
  input  [1:0] load_store_type,
  input  Clock,
  output [31:0] ReadData
);

  wire demultiplexer_1_out0, demultiplexer_1_out1, or_1_out, or_2_out;
  wire [0:0] xor_1_out;
  wire [1:0] AlignedAddress, xor_2_out;
  wire [7:0] ram_4_data;
  wire [31:8] ram_3_data;

  Demultiplexer #(.select(2), .enable("false")) demultiplexer_1 (
    .out0(demultiplexer_1_out0), .out1(demultiplexer_1_out1), .in(1'b1), .sel(load_store_type));  // open: out2, out3
  or or_1 (or_1_out, demultiplexer_1_out0, demultiplexer_1_out1);
  RAM #(.addrWidth(10), .bus("separate"), .Select("low")) ram_1 (
    .addr({Address[9:2], AlignedAddress}), .din(WriteData[31:24]), .data(ram_3_data[31:24]), .str(MemWrite),
    .sel(or_1_out), .clk(Clock), .ld(MemRead));  // open: clr
  or or_2 (or_2_out, demultiplexer_1_out0, demultiplexer_1_out1);
  RAM #(.addrWidth(10), .bus("separate"), .Select("low")) ram_2 (
    .addr({Address[9:2], AlignedAddress}), .din(WriteData[23:16]), .data(ram_3_data[23:16]), .str(MemWrite),
    .sel(or_2_out), .clk(Clock), .ld(MemRead));  // open: clr
  RAM #(.addrWidth(10), .bus("separate"), .Select("low")) ram_3 (
    .addr({Address[9:2], AlignedAddress}), .din(WriteData[15:8]), .data(ram_3_data[15:8]), .str(MemWrite),
    .sel(demultiplexer_1_out0), .clk(Clock), .ld(MemRead));  // open: clr
  RAM #(.addrWidth(10), .bus("separate"), .Select("low")) ram_4 (
    .addr({Address[9:2], AlignedAddress}), .din(WriteData[7:0]), .data(ram_4_data), .str(MemWrite),
    .clk(Clock), .ld(MemRead));  // open: sel, clr
  Multiplexer #(.select(2), .width(32), .enable("false")) multiplexer_1 (
    .in0({{24{1'b0}}, ram_4_data}), .in1({{16{1'b0}}, ram_3_data[15:8], ram_4_data}),
    .in2({ram_3_data, ram_4_data}), .out(ReadData), .sel(load_store_type));  // open: in3
  xor xor_1 (xor_1_out[0], Address[0], Address[0]);
  xor xor_2 (xor_2_out[0], Address[0], Address[0]);
  xor xor_3 (xor_2_out[1], Address[1], Address[1]);
  Multiplexer #(.select(2), .width(2), .enable("false")) multiplexer_2 (
    .in0(Address[1:0]), .in1({Address[1], xor_1_out[0]}), .in2(xor_2_out), .out(AlignedAddress),
    .sel(load_store_type));  // open: in3

  // Other names for the same wires on the sheet: AlignedAddress[9:2] = Address[9:2]

  // Notes on the sheet:
  //   Entradas
  //   Salidas
  //   Word
  //   Half Word
  //   Byte
  //   Alignment
endmodule
