// Logisim project ControlUnit_Multi-Cycle.circ as structural Verilog: 1 circuit, main circuit ControlUnit
module ControlUnit (
  input  [31:0] instr,
  input  Clock,
  output PCWrite,
  output IorD,
  output MemRead,
  output MemWrite,
  output IRWrite,
  output [1:0] PCSrc,
  output [3:0] ALUOp,
  output ALUSrcA,
  output [1:0] ALUSrcB,
  output RegWrite,
  output MemToReg,
  output [1:0] Imm,
  output PCWriteCond,
  output RegDst
);

  wire and_1_out, and_2_out, and_3_out, and_4_out, and_5_out, and_6_out, and_7_out, and_8_out, and_15_out,
       and_16_out, and_17_out, and_18_out, and_19_out, and_20_out, and_21_out, and_22_out, and_23_out,
       and_24_out, and_25_out, and_26_out, and_27_out, and_28_out, and_29_out, and_30_out, and_31_out,
       and_32_out, and_33_out, and_34_out, and_35_out, and_36_out, and_37_out, and_38_out, and_39_out,
       and_40_out, and_41_out, and_42_out, and_43_out, and_44_out, and_45_out, and_46_out, and_47_out,
       and_48_out, and_49_out, Branch_t, comparator_1_eq, comparator_2_eq, comparator_3_eq, comparator_4_eq,
       comparator_5_eq, comparator_6_eq, comparator_7_gt, comparator_8_gt, comparator_9_gt, comparator_10_gt,
       comparator_11_gt, comparator_12_gt, comparator_13_eq, comparator_14_eq, comparator_15_eq,
       demultiplexer_1_out1, demultiplexer_1_out2, demultiplexer_1_out3, Imm_t, Jump_t, Load_t, not_1_out,
       not_2_out, not_3_out, not_4_out, or_1_out, or_2_out, or_8_out, R_Type, Store_t;
  wire [1:0] Type;
  wire [2:0] Cycle_2_q, Cycle_3_q, Cycle_4_q, Cycle_5_q, Cycle_6_q, Cycle_q, flags_t;
  wire [3:0] bit_extender_1_out, bit_extender_2_out, transistor_3_out, transistor_4_out;
  wire [15:0] B_Flags, I_Flags, J_Flags, Load_Flags, R_Flags, Store_Flags;

  and and_1 (and_1_out, instr[0], instr[1], ~instr[2], ~instr[3]);  // AND_Gate
  and and_2 (and_2_out, instr[4], instr[5], ~instr[6]);  // AND_Gate
  and and_3 (and_3_out, instr[4], ~instr[5], ~instr[6]);  // AND_Gate
  and and_4 (and_4_out, ~instr[4], ~instr[5], ~instr[6]);  // AND_Gate
  and and_5 (and_5_out, ~instr[4], instr[5], ~instr[6]);  // AND_Gate
  and and_6 (and_6_out, ~instr[4], instr[5], instr[6]);  // AND_Gate
  and and_7 (and_7_out, instr[6], instr[5], ~instr[4]);  // AND_Gate
  and and_8 (and_8_out, instr[3], instr[2], instr[1], instr[0]);
  and and_9 (R_Type, and_1_out, and_2_out);
  and and_10 (Imm_t, and_1_out, and_3_out);
  and and_11 (Load_t, and_1_out, and_4_out);
  and and_12 (Store_t, and_1_out, and_5_out);
  and and_13 (Branch_t, and_1_out, and_6_out);
  and and_14 (Jump_t, and_7_out, and_8_out);
  and and_15 (and_15_out, R_Type, comparator_1_eq);
  and and_16 (and_16_out, Imm_t, comparator_2_eq);
  and and_17 (and_17_out, Load_t, comparator_3_eq);
  and and_18 (and_18_out, Store_t, comparator_4_eq);
  and and_19 (and_19_out, Branch_t, comparator_5_eq);
  and and_20 (and_20_out, Jump_t, comparator_6_eq);
  Counter #(.width(3), .max('h7)) Cycle (
    .Q(Cycle_q), .clk(Clock), .clr(and_15_out));  // open: load, D, count, carry, preset, down
  Counter #(.width(3), .max('h7)) Cycle_2 (
    .Q(Cycle_2_q), .clk(Clock), .clr(and_16_out));  // open: load, D, count, carry, preset, down
  Counter #(.width(3), .max('h7)) Cycle_3 (
    .Q(Cycle_3_q), .clk(Clock), .clr(and_17_out));  // open: load, D, count, carry, preset, down
  Counter #(.width(3), .max('h7)) Cycle_4 (
    .Q(Cycle_4_q), .clk(Clock), .clr(and_18_out));  // open: load, D, count, carry, preset, down
  Counter #(.width(3), .max('h7)) Cycle_5 (
    .Q(Cycle_5_q), .clk(Clock), .clr(and_19_out));  // open: load, D, count, carry, preset, down
  Counter #(.width(3), .max('h7)) Cycle_6 (
    .Q(Cycle_6_q), .clk(Clock), .clr(and_20_out));  // open: load, D, count, carry, preset, down
  Comparator #(.width(3)) comparator_1 (.a(Cycle_q), .b(3'b100), .eq(comparator_1_eq));  // open: gt, lt
  Comparator #(.width(3)) comparator_2 (.a(Cycle_2_q), .b(3'b100), .eq(comparator_2_eq));  // open: gt, lt
  Comparator #(.width(3)) comparator_3 (.a(Cycle_3_q), .b(3'b101), .eq(comparator_3_eq));  // open: gt, lt
  Comparator #(.width(3)) comparator_4 (.a(Cycle_4_q), .b(3'b100), .eq(comparator_4_eq));  // open: gt, lt
  or or_1 (or_1_out, Branch_t, Jump_t);
  Comparator #(.width(3)) comparator_5 (.a(Cycle_5_q), .b(3'b011), .eq(comparator_5_eq));  // open: gt, lt
  Comparator #(.width(3)) comparator_6 (.a(Cycle_6_q), .b(3'b011), .eq(comparator_6_eq));  // open: gt, lt
  or or_2 (or_2_out, Imm_t, Load_t, Store_t);
  or or_3 (flags_t[0], Imm_t, Store_t, Jump_t);
  or or_4 (flags_t[1], Store_t, Load_t);
  or or_5 (flags_t[2], Jump_t, Branch_t);
  Comparator #(.width(3)) comparator_7 (.a(Cycle_q), .b(3'b001), .gt(comparator_7_gt));  // open: eq, lt
  Comparator #(.width(3)) comparator_8 (.a(Cycle_2_q), .b(3'b001), .gt(comparator_8_gt));  // open: eq, lt
  Comparator #(.width(3)) comparator_9 (.a(Cycle_3_q), .b(3'b001), .gt(comparator_9_gt));  // open: eq, lt
  Comparator #(.width(3)) comparator_10 (.a(Cycle_4_q), .b(3'b001), .gt(comparator_10_gt));  // open: eq, lt
  Comparator #(.width(3)) comparator_11 (.a(Cycle_5_q), .b(3'b001), .gt(comparator_11_gt));  // open: eq, lt
  Comparator #(.width(3)) comparator_12 (.a(Cycle_6_q), .b(3'b001), .gt(comparator_12_gt));  // open: eq, lt
  or or_6 (Type[0], R_Type, or_1_out);
  or or_7 (Type[1], or_2_out, or_1_out);
  ROM #(.addrWidth(3), .dataWidth(16), .Select("low")) rom_1 (.addr(Cycle_q), .data(R_Flags));
  ROM #(.addrWidth(3), .dataWidth(16), .Select("low")) rom_2 (.addr(Cycle_2_q), .data(I_Flags));
  ROM #(.addrWidth(3), .dataWidth(16), .Select("low")) rom_3 (.addr(Cycle_3_q), .data(Load_Flags));
  ROM #(.addrWidth(3), .dataWidth(16), .Select("low")) rom_4 (.addr(Cycle_4_q), .data(Store_Flags));
  ROM #(.addrWidth(3), .dataWidth(16), .Select("low")) rom_5 (.addr(Cycle_5_q), .data(B_Flags));
  ROM #(.addrWidth(3), .dataWidth(16), .Select("low")) rom_6 (.addr(Cycle_6_q), .data(J_Flags));
  Demultiplexer #(.select(2), .enable("false")) demultiplexer_1 (
    .out1(demultiplexer_1_out1), .out2(demultiplexer_1_out2), .out3(demultiplexer_1_out3), .in(1'b1),
    .sel(Type));  // open: out0
  Comparator #(.width(7), .mode("unsigned")) comparator_13 (
    .a(instr[6:0]), .b(7'b0100011), .eq(comparator_13_eq));  // open: gt, lt
  Comparator #(.width(7), .mode("unsigned")) comparator_14 (
    .a(instr[6:0]), .b(7'b0000011), .eq(comparator_14_eq));  // open: gt, lt
  Comparator #(.width(7), .mode("unsigned")) comparator_15 (
    .a(instr[6:0]), .b(7'b1101111), .eq(comparator_15_eq));  // open: gt, lt
  or or_8 (or_8_out, comparator_13_eq, comparator_14_eq);
  Multiplexer #(.select(3), .width(16), .enable("false")) multiplexer_1 (
    .in0(R_Flags), .in1(I_Flags), .in2(Load_Flags), .in3(Store_Flags), .in4(B_Flags), .in5(J_Flags),
    .out({PCWrite, IorD, MemRead, MemWrite, IRWrite, PCSrc, ALUSrcA, ALUSrcB, RegWrite, MemToReg, Imm, PCWriteCond, RegDst}),
    .sel(flags_t));  // open: in6, in7
  and and_21 (and_21_out, ~instr[25], ~instr[26], ~instr[27], ~instr[28], ~instr[29], ~instr[30], ~instr[31]);  // AND_Gate
  and and_22 (and_22_out, ~instr[12], ~instr[13], ~instr[14]);  // AND_Gate
  and and_23 (and_23_out, instr[12], instr[13], instr[14]);
  and and_24 (and_24_out, ~instr[12], instr[13], instr[14]);  // AND_Gate
  and and_25 (and_25_out, ~instr[12], ~instr[13], instr[14]);  // AND_Gate
  and and_26 (and_26_out, instr[12], ~instr[13], ~instr[14]);  // AND_Gate
  and and_27 (and_27_out, instr[12], ~instr[13], instr[14]);  // AND_Gate
  and and_28 (and_28_out, ~instr[12], instr[13], ~instr[14]);  // AND_Gate
  and and_29 (and_29_out, instr[12], instr[13], ~instr[14]);  // AND_Gate
  and and_30 (and_30_out, ~instr[25], ~instr[26], ~instr[27], ~instr[28], ~instr[29], instr[30], ~instr[31]);  // AND_Gate
  and and_31 (and_31_out, ~instr[12], ~instr[13], ~instr[14]);  // AND_Gate
  and and_32 (and_32_out, instr[12], ~instr[13], instr[14]);  // AND_Gate
  and and_33 (and_33_out, instr[25], ~instr[26], ~instr[27], ~instr[28], ~instr[29], ~instr[30], ~instr[31]);  // AND_Gate
  and and_34 (and_34_out, ~instr[12], ~instr[13], ~instr[14]);  // AND_Gate
  and and_35 (and_35_out, ~instr[12], ~instr[13], instr[14]);  // AND_Gate
  assign bit_extender_1_out = {{3{1'b0}}, not_1_out};  // Bit_Extender bit_extender_1
  not not_1 (not_1_out, or_8_out);
  not not_2 (not_2_out, or_8_out);
  and and_36 (and_36_out, not_2_out, demultiplexer_1_out2);
  assign bit_extender_2_out = {{3{1'b0}}, not_3_out};  // Bit_Extender bit_extender_2
  not not_3 (not_3_out, comparator_15_eq);
  not not_4 (not_4_out, comparator_15_eq);
  and and_37 (and_37_out, not_4_out, demultiplexer_1_out3);
  and and_38 (and_38_out, and_21_out, and_22_out);
  and and_39 (and_39_out, and_21_out, and_23_out);
  and and_40 (and_40_out, and_21_out, and_24_out);
  and and_41 (and_41_out, and_21_out, and_25_out);
  and and_42 (and_42_out, and_21_out, and_26_out);
  and and_43 (and_43_out, and_21_out, and_27_out);
  and and_44 (and_44_out, and_21_out, and_28_out);
  and and_45 (and_45_out, and_21_out, and_29_out);
  and and_46 (and_46_out, and_30_out, and_31_out);
  and and_47 (and_47_out, and_30_out, and_32_out);
  and and_48 (and_48_out, and_33_out, and_34_out);
  and and_49 (and_49_out, and_33_out, and_35_out);
  Transistor #(.\type ("n"), .gate("br"), .width(4)) transistor_1 (
    .in(bit_extender_1_out), .out(ALUOp), .gate(or_8_out));
  Transistor #(.\type ("n"), .gate("br"), .width(4)) transistor_2 (
    .in(bit_extender_2_out), .out(ALUOp), .gate(comparator_15_eq));
  Transistor #(.\type ("n"), .width(4)) transistor_3 (.in(4'b0000), .out(transistor_3_out), .gate(and_38_out));
  Transistor #(.\type ("n"), .gate("br"), .width(4)) transistor_4 (
    .in(4'b0000), .out(transistor_4_out), .gate(and_22_out));
  Transistor #(.\type ("n"), .width(4)) transistor_5 (.in(4'b0100), .out(transistor_3_out), .gate(and_39_out));
  Transistor #(.\type ("n"), .gate("br"), .width(4)) transistor_6 (
    .in(4'b0100), .out(transistor_4_out), .gate(and_23_out));
  Transistor #(.\type ("n"), .width(4)) transistor_7 (.in(4'b1000), .out(transistor_3_out), .gate(and_40_out));
  Transistor #(.\type ("n"), .gate("br"), .width(4)) transistor_8 (
    .in(4'b1000), .out(transistor_4_out), .gate(and_24_out));
  Transistor #(.\type ("n"), .width(4)) transistor_9 (.in(4'b1001), .out(transistor_3_out), .gate(and_41_out));
  Transistor #(.\type ("n"), .gate("br"), .width(4)) transistor_10 (
    .in(4'b1001), .out(transistor_4_out), .gate(and_25_out));
  Transistor #(.\type ("n"), .width(4)) transistor_11 (.in(4'b1010), .out(transistor_3_out), .gate(and_42_out));
  Transistor #(.\type ("n"), .gate("br"), .width(4)) transistor_12 (
    .in(4'b1010), .out(transistor_4_out), .gate(and_42_out));
  Transistor #(.\type ("n"), .width(4)) transistor_13 (.in(4'b1011), .out(transistor_3_out), .gate(and_43_out));
  Transistor #(.\type ("n"), .gate("br"), .width(4)) transistor_14 (
    .in(4'b1011), .out(transistor_4_out), .gate(and_43_out));
  Transistor #(.\type ("n"), .width(4)) transistor_15 (.in(4'b1101), .out(transistor_3_out), .gate(and_44_out));
  Transistor #(.\type ("n"), .gate("br"), .width(4)) transistor_16 (
    .in(4'b1101), .out(transistor_4_out), .gate(and_28_out));
  Transistor #(.\type ("n"), .width(4)) transistor_17 (.in(4'b1110), .out(transistor_3_out), .gate(and_45_out));
  Transistor #(.\type ("n"), .gate("br"), .width(4)) transistor_18 (
    .in(4'b1110), .out(transistor_4_out), .gate(and_29_out));
  Transistor #(.\type ("n"), .width(4)) transistor_19 (.in(4'b0001), .out(transistor_3_out), .gate(and_46_out));
  Transistor #(.\type ("n"), .width(4)) transistor_20 (.in(4'b1100), .out(transistor_3_out), .gate(and_47_out));
  Transistor #(.\type ("n"), .gate("br"), .width(4)) transistor_21 (
    .in(4'b1100), .out(transistor_4_out), .gate(and_47_out));
  Transistor #(.\type ("n"), .width(4)) transistor_22 (.in(4'b0010), .out(transistor_3_out), .gate(and_48_out));
  Transistor #(.\type ("n"), .width(4)) transistor_23 (.in(4'b0011), .out(transistor_3_out), .gate(and_49_out));
  Transistor #(.\type ("n"), .gate("br"), .width(4)) transistor_24 (
    .in(transistor_3_out), .out(ALUOp), .gate(demultiplexer_1_out1));
  Transistor #(.\type ("n"), .gate("br"), .width(4)) transistor_25 (
    .in(transistor_4_out), .out(ALUOp), .gate(and_36_out));
  Transistor #(.\type ("n"), .gate("br"), .width(4)) transistor_26 (.in(4'b0001), .out(ALUOp), .gate(and_37_out));

  // Other names for the same wires on the sheet: OpCode[6:0] = instr[6:0]; OpCode4[3:0] = instr[3:0];
  //   OpCode3[2:0] = instr[6:4]; funct3[2:0] = instr[14:12]; funct7[6:0] = instr[31:25]

  // Notes on the sheet:
  //   Entradas
  //   Salidas
  //   Type-R
  //   Type-I
  //   Load
  //   Store
  //   Branch
  //   Jump
  //   Calcular Imm
  //   Type para calcular  ALUOp
  //   contents of rom_1 (hex, n*v repeats v):
  //   a840 a8c0 a980 a9a0
  //   contents of rom_2 (hex, n*v repeats v):
  //   a840 a8c0 a980 f980
  //   contents of rom_3 (hex, n*v repeats v):
  //   a840 a8c0 a980 e180 e1b0
  //   contents of rom_4 (hex, n*v repeats v):
  //   a840 a8c0 a980 f980
  //   contents of rom_5 (hex, n*v repeats v):
  //   a840 a8c0 ab04
  //   contents of rom_6 (hex, n*v repeats v):
  //   a840 a8c0 acc0
  //   Flags
  //   Funct7 = 0000000
  //   Funct7 = 0100000
  //   Funct7 = 0000001
  //   STORE
  //   LOAD
  //   JUMP/JAL
  //   ADD
  //   ADDI
  //   AND
  //   ANDI
  //   OR
  //   ORI
  //   XOR
  //   XORI
  //   SLL
  //   SLLI
  //   SRL
  //   SRLI
  //   SLT
  //   SLTI
  //   SLTU
  //   SLTUI
  //   SUB
  //   SRA
  //   SRAI
  //   MUL
  //   DIV
  //   BRANCH
endmodule
