// Logisim project Multi-Cycle.circ as structural Verilog: 2 circuits, main circuit Multi-cycle
module Multi_cycle (
);

  wire alu_1_zero, and_1_out, Clock, controlunit_1_alusrca, controlunit_1_iord, controlunit_1_irwrite,
       controlunit_1_memread, controlunit_1_memtoreg, controlunit_1_memwrite, controlunit_1_pcwrite,
       controlunit_1_pcwritecond, controlunit_1_regwrite, or_1_out;
  wire [1:0] controlunit_1_alusrcb, controlunit_1_imm, controlunit_1_pcsrc;
  wire [3:0] controlunit_1_aluop;
  wire [31:0] A_q, alu_1_resultado, ALUout_q, B_q, bit_extender_1_out, bit_extender_2_out,
       bit_extender_3_out, bit_extender_4_out, Instruction_Register_q, memory_1_readdata,
       Memory_Data_Register_q, multiplexer_1_out, multiplexer_2_out, multiplexer_3_out, multiplexer_4_out,
       multiplexer_5_out, multiplexer_6_out, PC_q, registerfile_1_d1, registerfile_1_d2;

  Clock clock_1 (.out(Clock));
  or or_1 (or_1_out, and_1_out, controlunit_1_pcwrite);
  Register #(.width(32), .Select("low")) PC (.D(multiplexer_6_out), .en(or_1_out), .Q(PC_q), .clk(Clock));  // open: clr
  Multiplexer #(.width(32), .enable("false")) multiplexer_1 (
    .in0(PC_q), .in1(ALUout_q), .out(multiplexer_1_out), .sel(controlunit_1_iord));
  Memory memory_1 (
    .Address(multiplexer_1_out), .WriteData(B_q), .MemRead(controlunit_1_memread),
    .MemWrite(controlunit_1_memwrite), .Clock(Clock), .ReadData(memory_1_readdata));
  Register #(.width(32), .Select("low")) Instruction_Register (
    .D(memory_1_readdata), .en(controlunit_1_irwrite), .Q(Instruction_Register_q), .clk(Clock));  // open: clr
  Register #(.width(32), .Select("low")) Memory_Data_Register (
    .D(memory_1_readdata), .Q(Memory_Data_Register_q), .clk(Clock));  // open: en, clr
  and and_1 (and_1_out, alu_1_zero, controlunit_1_pcwritecond);
  Multiplexer #(.width(32), .enable("false")) multiplexer_2 (
    .in0(ALUout_q), .in1(Memory_Data_Register_q), .out(multiplexer_2_out), .sel(controlunit_1_memtoreg));
  ControlUnit controlunit_1 (
    .instr(Instruction_Register_q), .ALUOp(controlunit_1_aluop), .ALUSrcB(controlunit_1_alusrcb),
    .PCWrite(controlunit_1_pcwrite), .MemRead(controlunit_1_memread), .MemWrite(controlunit_1_memwrite),
    .PCSrc(controlunit_1_pcsrc), .RegWrite(controlunit_1_regwrite), .MemToReg(controlunit_1_memtoreg),
    .Imm(controlunit_1_imm), .IorD(controlunit_1_iord), .IRWrite(controlunit_1_irwrite),
    .ALUSrcA(controlunit_1_alusrca), .Clock(Clock), .PCWriteCond(controlunit_1_pcwritecond));  // open: RegDst
  RegisterFile registerfile_1 (
    .Clock(Clock), .RegWrite(controlunit_1_regwrite), .rs1(Instruction_Register_q[19:15]),
    .rs2(Instruction_Register_q[24:20]), .Write_register(Instruction_Register_q[11:7]),
    .Write_data(multiplexer_2_out), .d1(registerfile_1_d1), .d2(registerfile_1_d2));
  assign bit_extender_1_out = {{20{1'b0}}, Instruction_Register_q[31:20]};  // Bit_Extender bit_extender_1
  assign bit_extender_2_out = {{20{1'b0}}, {Instruction_Register_q[31:25], Instruction_Register_q[11:7]}};  // Bit_Extender bit_extender_2
  assign bit_extender_3_out = {{11{1'b0}}, {Instruction_Register_q[31], Instruction_Register_q[19:12], Instruction_Register_q[20], Instruction_Register_q[30:21], 1'b0}};  // Bit_Extender bit_extender_3
  assign bit_extender_4_out = {{19{1'b0}}, {Instruction_Register_q[31], Instruction_Register_q[7], Instruction_Register_q[30:25], Instruction_Register_q[11:8], 1'b0}};  // Bit_Extender bit_extender_4
  Register #(.width(32), .Select("low")) A (.D(registerfile_1_d1), .Q(A_q), .clk(Clock));  // open: en, clr
  Register #(.width(32), .Select("low")) B (.D(registerfile_1_d2), .Q(B_q), .clk(Clock));  // open: en, clr
  Multiplexer #(.select(2), .width(32), .enable("false")) multiplexer_3 (
    .in0(bit_extender_1_out), .in1(bit_extender_2_out), .in3(bit_extender_3_out), .out(multiplexer_3_out),
    .sel(controlunit_1_imm));  // open: in2
  Multiplexer #(.width(32), .enable("false")) multiplexer_4 (
    .in0(PC_q), .in1(A_q), .out(multiplexer_4_out), .sel(controlunit_1_alusrca));
  Multiplexer #(.select(2), .width(32), .enable("false")) multiplexer_5 (
    .in0(B_q), .in1(32'h4), .in2(multiplexer_3_out), .in3(bit_extender_4_out), .out(multiplexer_5_out),
    .sel(controlunit_1_alusrcb));
  ALU alu_1 (
    .Operand1__rs1(multiplexer_4_out), .Operand2__rs2(multiplexer_5_out), .Control(controlunit_1_aluop),
    .Clock(Clock), .Resultado(alu_1_resultado), .Zero(alu_1_zero));
  Register #(.width(32), .Select("low")) ALUout (.D(alu_1_resultado), .Q(ALUout_q), .clk(Clock));  // open: en, clr
  Multiplexer #(.select(2), .width(32), .enable("false")) multiplexer_6 (
    .in0(alu_1_resultado), .in1(ALUout_q), .out(multiplexer_6_out), .sel(controlunit_1_pcsrc));  // open: in2, in3

  // Notes on the sheet:
  //   I-Type/Load
  //   Store
  //   Jump
  //   Branch
endmodule

module Memory (
  input  [31:0] Address,
  input  [31:0] WriteData,
  input  MemRead,
  input  MemWrite,
  input  Clock,
  output [31:0] ReadData
);

  RAM #(.dataWidth(32), .bus("separate"), .Select("low")) ram_1 (
    .addr(Address[9:2]), .din(WriteData), .data(ReadData), .str(MemWrite), .clk(Clock), .ld(MemRead));  // open: sel, clr

  // Notes on the sheet:
  //   Entradas
  //   Control
  //   Salida
endmodule
