// Logisim project Pipelined.circ as structural Verilog: 5 circuits, main circuit Pipeline
module Pipeline (
);

  wire ALU_greaterthanzero, ALU_lessthanzero, ALU_zero, and_1_out, Clock, ControlUnit_branchorjump,
       ControlUnit_memread, ControlUnit_memtoreg, ControlUnit_memwrite, ControlUnit_pcsrc,
       ControlUnit_regwrite, ControlUnit_signedop, EX_MEM_mem_greater_than, EX_MEM_mem_less_than,
       EX_MEM_mem_memread, EX_MEM_mem_memtoreg, EX_MEM_mem_memwrite, EX_MEM_mem_regwrite, EX_MEM_mem_zero,
       GE_out, ID_EX_ex_branchorjump, ID_EX_ex_memread, ID_EX_ex_memtoreg, ID_EX_ex_memwrite, ID_EX_ex_pcsrc,
       ID_EX_ex_regwrite, ID_EX_ex_signedop, MEM_WEB_wb_memtoreg, MEM_WEB_wb_regwrite, multiplexer_5_out,
       NE_out, not_1_out;
  wire [1:0] ControlUnit_alusrc, ControlUnit_branchcode, EX_MEM_mem_branchcode, ID_EX_ex_alusrc;
  wire [3:0] ControlUnit_aluop, ID_EX_ex_aluop;
  wire [4:0] EX_MEM_mem_write_register, ID_EX_ex_write_register, MEM_WEB_wb_write_register;
  wire [7:0] EX_MEM_mem_address;
  wire [31:0] adder_1_out, adder_2_out, ALU_resultado, bit_extender_1_out, bit_extender_2_out,
       bit_extender_3_out, bit_extender_4_out, Data_Memory_data, EX_MEM_mem_pc___4, EX_MEM_mem_write_data,
       ID_EX_ex_imm_branch, ID_EX_ex_imm_jump, ID_EX_ex_imm_lw_xl, ID_EX_ex_imm_sw, ID_EX_ex_pc___4,
       ID_EX_ex_rs1, ID_EX_ex_rs2, IF_ID_id_instruction, IF_ID_id_pc___4, Instruction_Memory_data,
       MEM_WEB_wb_address, MEM_WEB_wb_read_data, multiplexer_1_out, multiplexer_2_out, multiplexer_3_out,
       multiplexer_4_out, multiplexer_6_out, PC_q, RegisterFile_d1, RegisterFile_d2;
  wire [31:8] EX_MEM_mem_address_2;

  Clock clock_1 (.out(Clock));
  Multiplexer #(.width(32), .enable("false")) multiplexer_1 (
    .in0(adder_1_out), .in1(multiplexer_2_out), .out(multiplexer_1_out), .sel(ID_EX_ex_pcsrc));
  Register #(.width(32), .Select("low")) PC (.D(multiplexer_1_out), .Q(PC_q), .clk(Clock));  // open: en, clr
  Adder #(.width(32)) adder_1 (.a(32'h4), .b(PC_q), .out(adder_1_out));  // open: cin, cout
  ROM #(.dataWidth(32), .Select("low")) Instruction_Memory (.addr(PC_q[9:2]), .data(Instruction_Memory_data));
  IF_ID IF_ID (
    .IF_PC___4(adder_1_out), .IF_Instruction(Instruction_Memory_data), .Clock(Clock),
    .ID_PC___4(IF_ID_id_pc___4), .ID_Instruction(IF_ID_id_instruction));
  and and_1 (and_1_out, multiplexer_5_out, not_1_out);
  Multiplexer #(.width(32), .enable("false")) multiplexer_2 (
    .in0(EX_MEM_mem_pc___4), .in1(adder_2_out), .out(multiplexer_2_out), .sel(and_1_out));
  ControlUnit ControlUnit (
    .instr(IF_ID_id_instruction), .Clock(Clock), .MemToReg(ControlUnit_memtoreg),
    .RegWrite(ControlUnit_regwrite), .MemRead(ControlUnit_memread), .MemWrite(ControlUnit_memwrite),
    .BranchCode(ControlUnit_branchcode), .PCSrc(ControlUnit_pcsrc), .ALUOp(ControlUnit_aluop),
    .ALUSrc(ControlUnit_alusrc), .BranchOrJump(ControlUnit_branchorjump), .SignedOp(ControlUnit_signedop));
  assign bit_extender_1_out = {{20{1'b0}}, IF_ID_id_instruction[31:20]};  // Bit_Extender bit_extender_1
  assign bit_extender_2_out = {{20{1'b0}}, {IF_ID_id_instruction[31:25], IF_ID_id_instruction[11:7]}};  // Bit_Extender bit_extender_2
  assign bit_extender_3_out = {{20{1'b0}}, {IF_ID_id_instruction[31], IF_ID_id_instruction[7], IF_ID_id_instruction[30:26], IF_ID_id_instruction[11:8], 1'b0}};  // Bit_Extender bit_extender_3
  assign bit_extender_4_out = {{11{1'b0}}, {IF_ID_id_instruction[31], IF_ID_id_instruction[19:12], IF_ID_id_instruction[20], IF_ID_id_instruction[30:21], 1'b0}};  // Bit_Extender bit_extender_4
  not not_1 (not_1_out, ID_EX_ex_branchorjump);
  RegisterFile RegisterFile (
    .Clock(Clock), .RegWrite(MEM_WEB_wb_memtoreg), .rs1(IF_ID_id_instruction[19:15]),
    .rs2(IF_ID_id_instruction[24:20]), .Write_register(MEM_WEB_wb_write_register),
    .Write_data(multiplexer_6_out), .d1(RegisterFile_d1), .d2(RegisterFile_d2));
  ID_EX ID_EX (
    .ID_PC___4(IF_ID_id_pc___4), .ID_rs1(RegisterFile_d1), .ID_rs2(RegisterFile_d2),
    .ID_Imm_LW_xl(bit_extender_1_out), .ID_Imm_SW(bit_extender_2_out), .ID_Imm_Branch(bit_extender_3_out),
    .ID_Imm_Jump(bit_extender_4_out), .in_19(Clock), .EX_PC___4(ID_EX_ex_pc___4), .EX_rs1(ID_EX_ex_rs1),
    .EX_rs2(ID_EX_ex_rs2), .EX_Imm_LW_xl(ID_EX_ex_imm_lw_xl), .EX_Imm_SW(ID_EX_ex_imm_sw),
    .EX_Imm_Branch(ID_EX_ex_imm_branch), .EX_Imm_Jump(ID_EX_ex_imm_jump),
    .ID_Write_Register(IF_ID_id_instruction[11:7]), .EX_Write_Register(ID_EX_ex_write_register),
    .ID_MemToReg(ControlUnit_memtoreg), .ID_RegWrite(ControlUnit_regwrite), .ID_MemRead(ControlUnit_memread),
    .ID_MemWrite(ControlUnit_memwrite), .ID_BranchCode(ControlUnit_branchcode),
    .ID_BranchOrJump(ControlUnit_branchorjump), .ID_SignedOp(ControlUnit_signedop),
    .ID_ALUSrc(ControlUnit_alusrc), .ID_ALUOp(ControlUnit_aluop), .ID_PCSrc(ControlUnit_pcsrc),
    .EX_MemToReg(ID_EX_ex_memtoreg), .EX_RegWrite(ID_EX_ex_regwrite), .EX_MemRead(ID_EX_ex_memread),
    .EX_MemWrite(ID_EX_ex_memwrite), .EX_BranchCode(ControlUnit_branchcode),
    .EX_BranchOrJump(ID_EX_ex_branchorjump), .EX_PCSrc(ID_EX_ex_pcsrc), .EX_SignedOp(ID_EX_ex_signedop),
    .EX_ALUSrc(ID_EX_ex_alusrc), .EX_ALUOp(ID_EX_ex_aluop));
  Multiplexer #(.width(32), .enable("false")) multiplexer_3 (
    .in0(ID_EX_ex_imm_branch), .in1(ID_EX_ex_imm_jump), .out(multiplexer_3_out), .sel(ID_EX_ex_branchorjump));
  Adder #(.width(32)) adder_2 (.a(ID_EX_ex_pc___4), .b(multiplexer_3_out), .out(adder_2_out));  // open: cin, cout
  Multiplexer #(.select(2), .width(32), .enable("false")) multiplexer_4 (
    .in0(ID_EX_ex_rs2), .in1(ID_EX_ex_imm_lw_xl), .in2(ID_EX_ex_imm_sw), .out(multiplexer_4_out),
    .sel(ID_EX_ex_alusrc));  // open: in3
  ALU ALU (
    .Operand1__rs1(ID_EX_ex_rs1), .Operand2__rs2(multiplexer_4_out), .ALUOp(ID_EX_ex_aluop), .Clock(Clock),
    .Resultado(ALU_resultado), .Zero(ALU_zero), .LessThanZero(ALU_lessthanzero),
    .GreaterThanZero(ALU_greaterthanzero), .SignedCmp(ID_EX_ex_signedop));
  EX_MEM EX_MEM (
    .EX_PC___4(adder_2_out), .EX_Zero(ALU_zero), .EX_Address(ALU_resultado), .EX_Write_Data(ID_EX_ex_rs2),
    .EX_Write_Register(ID_EX_ex_write_register), .Clock(Clock), .MEM_PC___4(EX_MEM_mem_pc___4),
    .MEM_Zero(EX_MEM_mem_zero), .MEM_Address({EX_MEM_mem_address_2, EX_MEM_mem_address}),
    .MEM_Write_Data(EX_MEM_mem_write_data), .MEM_Write_Register(EX_MEM_mem_write_register),
    .EX_Less_Than(ALU_lessthanzero), .EX_Greater_Than(ALU_greaterthanzero),
    .MEM_Less_Than(EX_MEM_mem_less_than), .MEM_Greater_Than(EX_MEM_mem_greater_than),
    .EX_MemToReg(ID_EX_ex_memtoreg), .MEM_MemToReg(EX_MEM_mem_memtoreg), .EX_RegWrite(ID_EX_ex_regwrite),
    .MEM_RegWrite(EX_MEM_mem_regwrite), .EX_MemRead(ID_EX_ex_memread), .MEM_MemRead(EX_MEM_mem_memread),
    .EX_MemWrite(ID_EX_ex_memwrite), .MEM_MemWrite(EX_MEM_mem_memwrite),
    .EX_BranchCode(ControlUnit_branchcode), .MEM_BranchCode(EX_MEM_mem_branchcode));
  or GE (GE_out, EX_MEM_mem_greater_than, EX_MEM_mem_zero);
  or NE (NE_out, EX_MEM_mem_greater_than, EX_MEM_mem_less_than);
  Multiplexer #(.select(2), .enable("false")) multiplexer_5 (
    .in0(EX_MEM_mem_zero), .in1(NE_out), .in2(EX_MEM_mem_less_than), .in3(GE_out), .out(multiplexer_5_out),
    .sel(EX_MEM_mem_branchcode));
  RAM #(.dataWidth(32), .bus("separate"), .Select("low")) Data_Memory (
    .addr(EX_MEM_mem_address), .din(EX_MEM_mem_write_data), .data(Data_Memory_data),
    .str(EX_MEM_mem_memwrite), .clk(Clock), .ld(EX_MEM_mem_memread));  // open: sel, clr
  MEM_WB MEM_WEB (
    .MEM_Read_Data(Data_Memory_data), .MEM_Address({EX_MEM_mem_address_2, EX_MEM_mem_address}),
    .MEM_Write_Register(EX_MEM_mem_write_register), .Clock(Clock), .WB_Read_Data(MEM_WEB_wb_read_data),
    .WB_Address(MEM_WEB_wb_address), .WB_Write_Register(MEM_WEB_wb_write_register),
    .MEM_MemToReg(EX_MEM_mem_memtoreg), .WB_MemToReg(MEM_WEB_wb_memtoreg),
    .MEM_RegWrite(EX_MEM_mem_regwrite), .WB_RegWrite(MEM_WEB_wb_regwrite));
  Multiplexer #(.width(32), .enable("false")) multiplexer_6 (
    .in0(MEM_WEB_wb_address), .in1(MEM_WEB_wb_read_data), .out(multiplexer_6_out), .sel(MEM_WEB_wb_regwrite));

  // Notes on the sheet:
  //   I-Type/Load
  //   S-Type
  //   Branch
  //   Jump
  //   Write Register
endmodule

module IF_ID (
  input  [31:0] IF_PC___4,
  input  [31:0] IF_Instruction,
  input  Clock,
  output [31:0] ID_PC___4,
  output [31:0] ID_Instruction
);

  Register #(.width(32), .Select("low")) register_1 (.D(IF_PC___4), .Q(ID_PC___4), .clk(Clock));  // open: en, clr
  Register #(.width(32), .Select("low")) register_2 (
    .D(IF_Instruction), .Q(ID_Instruction), .clk(Clock));  // open: en, clr

  // Other names for the same wires on the sheet: ID_Instr[31:0] = ID_Instruction; ID_PC_4[31:0] = ID_PC___4;
  //   IF_Instr[31:0] = IF_Instruction; IF_PC_4[31:0] = IF_PC___4

  // Notes on the sheet:
  //   Control
endmodule

module ID_EX (
  input  [31:0] ID_PC___4,
  input  [31:0] ID_rs1,
  input  [31:0] ID_rs2,
  input  [31:0] ID_Imm_LW_xl,
  input  [31:0] ID_Imm_SW,
  input  [31:0] ID_Imm_Branch,
  input  [31:0] ID_Imm_Jump,
  input  [4:0] ID_Write_Register,
  input  ID_MemToReg,
  input  ID_RegWrite,
  input  ID_MemRead,
  input  ID_MemWrite,
  input  [1:0] ID_BranchCode,
  input  [3:0] ID_ALUOp,
  input  [1:0] ID_ALUSrc,
  input  ID_BranchOrJump,
  input  ID_PCSrc,
  input  ID_SignedOp,
  input  in_19,
  output [31:0] EX_PC___4,
  output [31:0] EX_rs1,
  output [31:0] EX_rs2,
  output [31:0] EX_Imm_LW_xl,
  output [31:0] EX_Imm_SW,
  output [31:0] EX_Imm_Branch,
  output [31:0] EX_Imm_Jump,
  output [4:0] EX_Write_Register,
  output EX_MemToReg,
  output EX_RegWrite,
  output EX_MemRead,
  output EX_MemWrite,
  output [1:0] EX_BranchCode,
  output [3:0] EX_ALUOp,
  output [1:0] EX_ALUSrc,
  output EX_BranchOrJump,
  output EX_PCSrc,
  output EX_SignedOp
);

  Register #(.width(32), .Select("low")) register_1 (.D(ID_PC___4), .Q(EX_PC___4), .clk(in_19));  // open: en, clr
  Register #(.width(32), .Select("low")) register_2 (.D(ID_rs1), .Q(EX_rs1), .clk(in_19));  // open: en, clr
  Register #(.width(32), .Select("low")) register_3 (.D(ID_rs2), .Q(EX_rs2), .clk(in_19));  // open: en, clr
  Register #(.width(32), .Select("low")) register_4 (.D(ID_Imm_LW_xl), .Q(EX_Imm_LW_xl), .clk(in_19));  // open: en, clr
  Register #(.width(32), .Select("low")) register_5 (.D(ID_Imm_SW), .Q(EX_Imm_SW), .clk(in_19));  // open: en, clr
  Register #(.width(32), .Select("low")) register_6 (
    .D(ID_Imm_Branch), .Q(EX_Imm_Branch), .clk(in_19));  // open: en, clr
  Register #(.width(32), .Select("low")) register_7 (.D(ID_Imm_Jump), .Q(EX_Imm_Jump), .clk(in_19));  // open: en, clr
  Register #(.width(5), .Select("low")) register_8 (
    .D(ID_Write_Register), .Q(EX_Write_Register), .clk(in_19));  // open: en, clr
  Register #(.width(1), .Select("low")) register_9 (.D(ID_MemToReg), .Q(EX_MemToReg), .clk(in_19));  // open: en, clr
  Register #(.width(1), .Select("low")) register_10 (.D(ID_RegWrite), .Q(EX_RegWrite), .clk(in_19));  // open: en, clr
  Register #(.width(1), .Select("low")) register_11 (.D(ID_MemRead), .Q(EX_MemRead), .clk(in_19));  // open: en, clr
  Register #(.width(1), .Select("low")) register_12 (.D(ID_MemWrite), .Q(EX_MemWrite), .clk(in_19));  // open: en, clr
  Register #(.width(2), .Select("low")) register_13 (
    .D(ID_BranchCode), .Q(EX_BranchCode), .clk(in_19));  // open: en, clr
  Register #(.width(4), .Select("low")) register_14 (.D(ID_ALUOp), .Q(EX_ALUOp), .clk(in_19));  // open: en, clr
  Register #(.width(2), .Select("low")) register_15 (.D(ID_ALUSrc), .Q(EX_ALUSrc), .clk(in_19));  // open: en, clr
  Register #(.width(1), .Select("low")) register_16 (
    .D(ID_BranchOrJump), .Q(EX_BranchOrJump), .clk(in_19));  // open: en, clr
  Register #(.width(1), .Select("low")) register_17 (.D(ID_PCSrc), .Q(EX_PCSrc), .clk(in_19));  // open: en, clr
  Register #(.width(1), .Select("low")) register_18 (.D(ID_SignedOp), .Q(EX_SignedOp), .clk(in_19));  // open: en, clr

  // Other names for the same wires on the sheet: Clock = in_19; SignedOp = ID_SignedOp

  // Notes on the sheet:
  //   Entradas
  //   WB Flags
  //   Mem Flags
  //   EX Flags
  //   Salidas
  //   WB Flags
  //   Mem Flags
  //   EX Flags
endmodule

module EX_MEM (
  input  [31:0] EX_PC___4,
  input  EX_Zero,
  input  EX_Less_Than,
  input  EX_Greater_Than,
  input  [31:0] EX_Address,
  input  [31:0] EX_Write_Data,
  input  [4:0] EX_Write_Register,
  input  EX_MemToReg,
  input  EX_RegWrite,
  input  EX_MemRead,
  input  EX_MemWrite,
  input  [1:0] EX_BranchCode,
  input  Clock,
  output [31:0] MEM_PC___4,
  output MEM_Zero,
  output MEM_Less_Than,
  output MEM_Greater_Than,
  output [31:0] MEM_Address,
  output [31:0] MEM_Write_Data,
  output [4:0] MEM_Write_Register,
  output MEM_MemToReg,
  output MEM_RegWrite,
  output MEM_MemRead,
  output MEM_MemWrite,
  output [1:0] MEM_BranchCode
);

  Register #(.width(32), .Select("low")) register_1 (.D(EX_PC___4), .Q(MEM_PC___4), .clk(Clock));  // open: en, clr
  Register #(.width(1), .Select("low")) register_2 (.D(EX_Zero), .Q(MEM_Zero), .clk(Clock));  // open: en, clr
  Register #(.width(1), .Select("low")) register_3 (.D(EX_Less_Than), .Q(MEM_Less_Than), .clk(Clock));  // open: en, clr
  Register #(.width(1), .Select("low")) register_4 (
    .D(EX_Greater_Than), .Q(MEM_Greater_Than), .clk(Clock));  // open: en, clr
  Register #(.width(32), .Select("low")) register_5 (.D(EX_Address), .Q(MEM_Address), .clk(Clock));  // open: en, clr
  Register #(.width(32), .Select("low")) register_6 (
    .D(EX_Write_Data), .Q(MEM_Write_Data), .clk(Clock));  // open: en, clr
  Register #(.width(5), .Select("low")) register_7 (
    .D(EX_Write_Register), .Q(MEM_Write_Register), .clk(Clock));  // open: en, clr
  Register #(.width(1), .Select("low")) register_8 (.D(EX_MemToReg), .Q(MEM_MemToReg), .clk(Clock));  // open: en, clr
  Register #(.width(1), .Select("low")) register_9 (.D(EX_RegWrite), .Q(MEM_RegWrite), .clk(Clock));  // open: en, clr
  Register #(.width(1), .Select("low")) register_10 (.D(EX_MemRead), .Q(MEM_MemRead), .clk(Clock));  // open: en, clr
  Register #(.width(1), .Select("low")) register_11 (.D(EX_MemWrite), .Q(MEM_MemWrite), .clk(Clock));  // open: en, clr
  Register #(.width(2), .Select("low")) register_12 (
    .D(EX_BranchCode), .Q(MEM_BranchCode), .clk(Clock));  // open: en, clr

  // Notes on the sheet:
  //   WB Flags
  //   Mem Flags
  //   WB Flags
  //   Mem Flags
endmodule

module MEM_WB (
  input  [31:0] MEM_Read_Data,
  input  [31:0] MEM_Address,
  input  [4:0] MEM_Write_Register,
  input  MEM_MemToReg,
  input  MEM_RegWrite,
  input  Clock,
  output [31:0] WB_Read_Data,
  output [31:0] WB_Address,
  output [4:0] WB_Write_Register,
  output WB_MemToReg,
  output WB_RegWrite
);

  Register #(.width(32), .Select("low")) register_1 (
    .D(MEM_Read_Data), .Q(WB_Read_Data), .clk(Clock));  // open: en, clr
  Register #(.width(32), .Select("low")) register_2 (.D(MEM_Address), .Q(WB_Address), .clk(Clock));  // open: en, clr
  Register #(.width(5), .Select("low")) register_3 (
    .D(MEM_Write_Register), .Q(WB_Write_Register), .clk(Clock));  // open: en, clr
  Register #(.width(1), .Select("low")) register_4 (.D(MEM_MemToReg), .Q(WB_MemToReg), .clk(Clock));  // open: en, clr
  Register #(.width(1), .Select("low")) register_5 (.D(MEM_RegWrite), .Q(WB_RegWrite), .clk(Clock));  // open: en, clr

  // Notes on the sheet:
  //   WB Flags
  //   WB Flags
endmodule
