// Logisim project Single-Cycle.circ as structural Verilog: 2 circuits, main circuit main
module main (
);

  wire alu_1_zero, and_1_out, Clock_out, controlunit_1_alusrc, controlunit_1_jump, controlunit_1_memread,
       controlunit_1_memtoreg, controlunit_1_memwrite, controlunit_1_pcsrc, controlunit_1_regwrite,
       fivestagesclock_1_clock_1, fivestagesclock_1_clock_2, fivestagesclock_1_clock_3,
       fivestagesclock_1_clock_4, fivestagesclock_1_clock_5, fivestagesclock_1_start, or_1_out;
  wire [1:0] controlunit_1_immcontrol;
  wire [3:0] controlunit_1_aluop;
  wire [4:0] register_1_q_2;
  wire [31:0] adder_1_out, adder_2_out, alu_1_resultado, bit_extender_1_out, bit_extender_2_out,
       bit_extender_3_out, bit_extender_4_out, Data_Memory_data, Instruction_memory_data, multiplexer_1_out,
       multiplexer_3_out, multiplexer_4_out, multiplexer_5_out, PC_q, register_1_q, register_2_q,
       register_3_q, register_4_q, register_5_q, registerfile_1_d1, registerfile_1_d2, shifter_1_out,
       Write_Data;

  Register #(.width(32), .Select("low")) PC (
    .D(multiplexer_4_out), .Q(PC_q), .clk(fivestagesclock_1_clock_1), .clr(fivestagesclock_1_start));  // open: en
  Clock Clock (.out(Clock_out));
  Adder #(.width(32)) adder_1 (.a(32'h4), .b(PC_q), .out(adder_1_out));  // open: cin, cout
  FiveStagesClock fivestagesclock_1 (
    .in_1(Clock_out), .Start(fivestagesclock_1_start), .Clock_1(fivestagesclock_1_clock_1),
    .Clock_2(fivestagesclock_1_clock_2), .Clock_3(fivestagesclock_1_clock_3),
    .Clock_4(fivestagesclock_1_clock_4), .Clock_5(fivestagesclock_1_clock_5));
  ROM #(.dataWidth(32), .Select("low")) Instruction_memory (.addr(PC_q[9:2]), .data(Instruction_memory_data));
  Register #(.width(32), .Select("low")) register_1 (
    .D(Instruction_memory_data), .Q({register_1_q[31:25], register_1_q_2, register_1_q[19:0]}),
    .clk(fivestagesclock_1_clock_2));  // open: en, clr
  Shifter #(.width(32)) shifter_1 (
    .in({register_1_q[31:25], register_1_q_2, register_1_q[19:0]}), .\dist (5'b00010), .out(shifter_1_out));
  ControlUnit controlunit_1 (
    .instr({register_1_q[31:25], register_1_q_2, register_1_q[19:0]}), .ALUOp(controlunit_1_aluop),
    .ALUSrc(controlunit_1_alusrc), .Jump(controlunit_1_jump), .MemRead(controlunit_1_memread),
    .MemWrite(controlunit_1_memwrite), .PCSrc(controlunit_1_pcsrc), .RegWrite(controlunit_1_regwrite),
    .MemToReg(controlunit_1_memtoreg), .ImmControl(controlunit_1_immcontrol));
  assign bit_extender_1_out = {{20{1'b0}}, {register_1_q[31:25], register_1_q_2}};  // Bit_Extender bit_extender_1
  assign bit_extender_2_out = {{20{1'b0}}, {register_1_q[31:25], register_1_q[11:7]}};  // Bit_Extender bit_extender_2
  assign bit_extender_3_out = {{20{1'b0}}, {register_1_q[31], register_1_q[7], register_1_q[30:26], register_1_q[11:8], 1'b0}};  // Bit_Extender bit_extender_3
  assign bit_extender_4_out = {{11{1'b0}}, {register_1_q[31], register_1_q[19:12], register_1_q_2[0], register_1_q[30:25], register_1_q_2[4:1], 1'b0}};  // Bit_Extender bit_extender_4
  or or_1 (or_1_out, fivestagesclock_1_clock_3, fivestagesclock_1_clock_5);
  RegisterFile registerfile_1 (
    .Clock(or_1_out), .RegWrite(controlunit_1_regwrite), .rs1(register_1_q[19:15]), .rs2(register_1_q_2),
    .Write_register(register_1_q[11:7]), .Write_data(register_5_q), .d1(registerfile_1_d1),
    .d2(registerfile_1_d2));
  Register #(.width(32), .Select("low")) register_2 (
    .D(registerfile_1_d1), .Q(register_2_q), .clk(fivestagesclock_1_clock_3));  // open: en, clr
  Register #(.width(32), .Select("low")) register_3 (
    .D(registerfile_1_d2), .Q(register_3_q), .clk(fivestagesclock_1_clock_3));  // open: en, clr
  Multiplexer #(.select(2), .width(32), .enable("false")) multiplexer_1 (
    .in0(bit_extender_1_out), .in1(bit_extender_2_out), .in2(bit_extender_3_out), .in3(bit_extender_4_out),
    .out(multiplexer_1_out), .sel(controlunit_1_immcontrol));
  Multiplexer #(.width(32), .enable("false")) multiplexer_2 (
    .in0(register_3_q), .in1(multiplexer_1_out), .out(Write_Data), .sel(controlunit_1_alusrc));
  ALU alu_1 (
    .Operand1__rs1(register_2_q), .Operand2__rs2(Write_Data), .Control(controlunit_1_aluop),
    .Clock(fivestagesclock_1_clock_4), .Resultado(alu_1_resultado), .Zero(alu_1_zero));
  Register #(.width(32), .Select("low")) register_4 (
    .D(alu_1_resultado), .Q(register_4_q), .clk(fivestagesclock_1_clock_4));  // open: en, clr
  Adder #(.width(32)) adder_2 (.a(adder_1_out), .b(bit_extender_3_out), .out(adder_2_out));  // open: cin, cout
  and and_1 (and_1_out, controlunit_1_pcsrc, alu_1_zero);
  Multiplexer #(.width(32), .enable("false")) multiplexer_3 (
    .in0(adder_1_out), .in1(adder_2_out), .out(multiplexer_3_out), .sel(and_1_out));
  Multiplexer #(.width(32), .enable("false")) multiplexer_4 (
    .in0(multiplexer_3_out), .in1(shifter_1_out), .out(multiplexer_4_out), .sel(controlunit_1_jump));
  RAM #(.dataWidth(32), .bus("separate"), .Select("low")) Data_Memory (
    .addr(register_4_q[7:0]), .din(Write_Data), .data(Data_Memory_data), .str(controlunit_1_memwrite),
    .clk(fivestagesclock_1_clock_5), .ld(controlunit_1_memread));  // open: sel, clr
  Register #(.width(32), .Select("low")) register_5 (
    .D(multiplexer_5_out), .Q(register_5_q), .clk(fivestagesclock_1_clock_5));  // open: en, clr
  Multiplexer #(.width(32), .enable("false")) multiplexer_5 (
    .in0(register_4_q), .in1(Data_Memory_data), .out(multiplexer_5_out), .sel(controlunit_1_memtoreg));

  // Notes on the sheet:
  //   S2
  //   S1
  //   Start
  //   S5
  //   S3
  //   S4
  //   R-Type
  //   I-Type/Load
  //   Store
  //   Branch
  //   Jump
endmodule

module FiveStagesClock (
  input  in_1,
  output Start,
  output Clock_1,
  output Clock_2,
  output Clock_3,
  output Clock_4,
  output Clock_5
);

  wire [7:0] counter_1_q, divider_1_rem;

  Counter counter_1 (.Q(counter_1_q), .clk(in_1));  // open: load, D, count, carry, clr, preset, down
  Divider divider_1 (.a(counter_1_q), .b(8'h5), .rem(divider_1_rem));  // open: out, upper
  Demultiplexer #(.select(3), .enable("false")) demultiplexer_1 (
    .out0(Clock_1), .out1(Clock_2), .out2(Clock_3), .out3(Clock_4), .out4(Clock_5), .in(in_1),
    .sel(divider_1_rem[2:0]));  // open: out5, out6, out7
  Comparator comparator_1 (.a({8{1'b0}}), .b(counter_1_q), .eq(Start));  // open: gt, lt

  // Other names for the same wires on the sheet: Clock = in_1

  // Notes on the sheet:
  //   Entrada
  //   Salidas
endmodule
